// Logisim project 单周期多级中断.circ as structural Verilog: 5 circuits, main circuit cpu
module cpu (
);

  wire ALUSrc, and_1_out, and_2_out, and_3_out, and_4_out, and_5_out, and_6_out, beq, bgez, bne, clk,
       epcRead, epcWE, equal, eret, go, ieWE, IR1, IR2, IR3, Jal, Jr, Jump, lh, MemRead, MemWrite, not_1_out,
       not_2_out, or_1_out, or_2_out, or_3_out, or_4_out, RegDst, RegWrite, RST, shift, syscall, W1, W2, W3,
       Zero_extend, \停机 ;
  wire [3:0] control_1_aluop;
  wire [4:0] decoder_1_ra, decoder_1_rb, decoder_1_rw;
  wire [5:0] decoder_1_funct, decoder_1_opcode;
  wire [15:0] \总周期数 , \无条件分支指令数 , \有条件分支成功跳转 , \有条件分支指令数 ;
  wire [19:0] alu_1_result_2;
  wire [27:0] decoder_1_pcjump;
  wire [31:0] alu_1_result, dA, epc, epcw, extendImm, interrupt_1_next_pc, mips_ram_1_p8, multiplexer_1_out,
       multiplexer_2_out, multiplexer_3_out, multiplexer_4_out, multiplexer_6_out, multiplexer_7_out,
       npc_1_nextpc, npc_1_pcjar, pc_q, rom_1_data, SyscallOut;
  wire [31:16] multiplexer_5_out;

  Button \u_总复位  (.out(RST));
  Button _1 (.out(IR1));
  Button _2 (.out(IR2));
  Button _3 (.out(IR3));
  Button u_go (.out(go));
  LED led_1 (.in(W1));
  LED led_2 (.in(W2));
  LED led_3 (.in(W3));
  Hex_Digit_Display hex_digit_display_1 (.value(SyscallOut[31:28]));  // open: dp
  Hex_Digit_Display hex_digit_display_2 (.value(SyscallOut[27:24]));  // open: dp
  Npc npc_1 (
    .PCjmp(decoder_1_pcjump), .jump(Jump), .extendIMM(extendImm), .bne(bne), .beq(beq), .PC(pc_q), .jr(Jr),
    .PCjar(npc_1_pcjar), .dA(dA), .equal(equal), .NextPc(npc_1_nextpc), .bgez(bgez));
  Interrupt interrupt_1 (
    .clk(clk), .cur_pc(npc_1_nextpc), .IR1(IR1), .IR2(IR2), .IR3(IR3), .ERET(eret),
    .next_pc(interrupt_1_next_pc), .IEW(ieWE), .epc(epc), .epc_w_v(epcw), .epc_w_en(epcWE), .IE_V(epcw),
    .led1(W1), .led2(W2), .led3(W3));
  not not_1 (not_1_out, \停机 );
  Hex_Digit_Display hex_digit_display_3 (.value(SyscallOut[23:20]));  // open: dp
  Hex_Digit_Display hex_digit_display_4 (.value(SyscallOut[19:16]));  // open: dp
  Register #(.width(32)) pc (.D(interrupt_1_next_pc), .en(not_1_out), .Q(pc_q), .clk(clk), .clr(RST));
  Hex_Digit_Display hex_digit_display_5 (.value(SyscallOut[11:8]));  // open: dp
  Hex_Digit_Display hex_digit_display_6 (.value(SyscallOut[15:12]));  // open: dp
  Hex_Digit_Display hex_digit_display_7 (.value(SyscallOut[7:4]));  // open: dp
  Hex_Digit_Display hex_digit_display_8 (.value(SyscallOut[3:0]));  // open: dp
  Clock clock_1 (.out(clk));
  ROM #(.addrWidth(10), .dataWidth(32)) rom_1 (.addr(pc_q[11:2]), .data(rom_1_data));  // open: sel
  Multiplexer #(.width(32), .enable("false")) multiplexer_1 (
    .in0(multiplexer_6_out), .in1(epc), .out(multiplexer_1_out), .sel(epcRead));
  Decoder decoder_1 (
    .CODE(rom_1_data), .PCjump(decoder_1_pcjump), .OPCODE(decoder_1_opcode), .FUNCT(decoder_1_funct),
    .RA(decoder_1_ra), .RB(decoder_1_rb), .RW(decoder_1_rw), .shift(shift), .RegDst(RegDst),
    .syscall(syscall), .Jal(Jal), .Zero_extend(Zero_extend), .extend(extendImm));
  Multiplexer #(.width(32), .enable("false")) multiplexer_2 (
    .in0(multiplexer_1_out), .in1(npc_1_pcjar), .out(multiplexer_2_out), .sel(Jal));
  // Probe on \总周期数 
  // Probe on \无条件分支指令数 
  // Probe on \有条件分支指令数 
  // Probe on \有条件分支成功跳转 
  // Probe on decoder_1_rw
  // Probe on decoder_1_ra
  // RegisterFile registerfile_1: pin names not known; wires that end beside it: multiplexer_2_out, clk, RegWrite, decoder_1_rw, decoder_1_ra, decoder_1_rb, dA, epcw
  // Probe on decoder_1_rb
  and and_1 (and_1_out, bne, ~equal);  // AND_Gate
  and and_2 (and_2_out, equal, beq);
  Multiplexer #(.width(32), .enable("false")) multiplexer_3 (
    .in0(epcw), .in1(extendImm), .out(multiplexer_3_out), .sel(ALUSrc));
  or or_1 (or_1_out, Jal, Jump, Jr);
  or or_2 (or_2_out, bne, beq, bgez);
  or or_3 (or_3_out, and_1_out, and_2_out);
  Multiplexer #(.width(32), .enable("false")) multiplexer_4 (
    .in0(multiplexer_3_out), .in1(32'ha), .out(multiplexer_4_out), .sel(syscall));
  Control control_1 (
    .ALUOP(control_1_aluop), .shift(shift), .Zero_extend(Zero_extend), .ALUSrc(ALUSrc), .RegDst(RegDst),
    .RegWrite(RegWrite), .Jump(Jump), .beq(beq), .bne(bne), .MemRead(MemRead), .MemWrite(MemWrite),
    .Jal(Jal), .jr(Jr), .syscall(syscall), .bgez(bgez), .OPCODE(decoder_1_opcode), .FUNCT(decoder_1_funct),
    .lh(lh), .eret(eret), .IR(rom_1_data), .EpcRead(epcRead), .EpcWE(epcWE), .IEWE(ieWE));
  Counter #(.width(16), .max('hffff)) counter_1 (
    .count(and_3_out), .Q(\无条件分支指令数 ), .clk(clk), .clr(RST));  // open: load, D, carry
  and and_3 (and_3_out, or_1_out, ~\停机 );  // AND_Gate
  Counter #(.width(16), .max('hffff)) counter_2 (
    .count(and_4_out), .Q(\有条件分支指令数 ), .clk(clk), .clr(RST));  // open: load, D, carry
  and and_4 (and_4_out, or_2_out, ~\停机 );  // AND_Gate
  Counter #(.width(16), .max('hffff)) counter_3 (
    .count(and_5_out), .Q(\有条件分支成功跳转 ), .clk(clk), .clr(RST));  // open: load, D, carry
  and and_5 (and_5_out, ~\停机 , or_3_out);  // AND_Gate
  ALU alu_1 (
    .AluOP(control_1_aluop), .X(dA), .Equal(equal),
    .Result({alu_1_result[31:22], alu_1_result_2, alu_1_result[1:0]}), .Y(multiplexer_4_out));  // open: Signed_Overflow, Result_2, UnSigned_Overflow
  // Probe on {alu_1_result[31:22], alu_1_result_2, alu_1_result[1:0]}
  Register #(.width(32)) register_1 (.D(epcw), .en(and_6_out), .Q(SyscallOut), .clk(clk), .clr(RST));
  and and_6 (and_6_out, ~equal, syscall);  // AND_Gate
  Register #(.width(1)) register_2 (.D(equal), .en(syscall), .Q(\停机 ), .clk(clk), .clr(or_4_out));
  or or_4 (or_4_out, RST, go);
  Multiplexer #(.width(32), .enable("false")) multiplexer_5 (
    .in0({alu_1_result[31:22], alu_1_result_2, alu_1_result[1:0]}), .in1(mips_ram_1_p8),
    .out({multiplexer_5_out, multiplexer_7_out[15:0]}), .sel(MemRead));
  // MIPS_RAM mips_ram_1: pin names not known; wires that end beside it: {alu_1_result[31:22], alu_1_result_2, alu_1_result[1:0]}, alu_1_result_2, epcw, MemWrite, clk, MemRead, RST, mips_ram_1_p8
  Multiplexer #(.width(32), .enable("false")) multiplexer_6 (
    .in0({multiplexer_5_out, multiplexer_7_out[15:0]}), .in1(multiplexer_7_out), .out(multiplexer_6_out),
    .sel(lh));
  not not_2 (not_2_out, \停机 );
  Pull_Resistor pull_resistor_1 (.node(multiplexer_7_out[15]));
  Multiplexer #(.width(16), .enable("false")) multiplexer_7 (
    .in0({16{1'b0}}), .in1({16{1'b1}}), .out(multiplexer_7_out[31:16]), .sel(multiplexer_7_out[15]));
  Counter #(.width(16), .max('hffff)) counter_4 (
    .count(not_2_out), .Q(\总周期数 ), .clk(clk), .clr(RST));  // open: load, D, carry

  // Other names for the same wires on the sheet: ieW[31:0] = epcw

  // Notes on the sheet:
  //   数码管输出应该用寄存器锁存，否则显示数据只能一闪而过
  //   可以通过项目增加Logisim库的方式将前几次实验完成的电路作为子电路引入到本电路中使用
  //   指令存储器
  //   数码管输出
  //   contents of rom_1 (hex, n*v repeats v):
  //   201d0300 2008000a 8000c84 8000c06 8000c30 8000c5a 23bdfffc afa80000 23bdfffc afa90000 23bdfffc
  //   afb00000 23bdfffc afb10000 23bdfffc afa40000 23bdfffc afa20000 40080800 23bdfffc afa80000 20080000
  //   40880000 20110001 118020 108100 102020 20020022 c 1600fffb 20080001 40880000 8fa80000 23bd0004
  //   40880800 8fa20000 23bd0004 8fa40000 23bd0004 8fb10000 23bd0004 8fb00000 23bd0004 8fa90000 23bd0004
  //   8fa80000 23bd0004 42000018 23bdfffc afa80000 23bdfffc afa90000 23bdfffc afb00000 23bdfffc afb10000
  //   23bdfffc afa40000 23bdfffc afa20000 40080800 23bdfffc afa80000 20080000 40880000 20110002 118020
  //   108100 102020 20020022 c 1600fffb 20080001 40880000 8fa80000 23bd0004 40880800 8fa20000 23bd0004
  //   8fa40000 23bd0004 8fb10000 23bd0004 8fb00000 23bd0004 8fa90000 23bd0004 8fa80000 23bd0004 42000018
  //   23bdfffc afa80000 23bdfffc afa90000 23bdfffc afb00000 23bdfffc afb10000 23bdfffc afa40000 23bdfffc
  //   afa20000 40080800 23bdfffc afa80000 20080000 40880000 20110003 118020 108100 102020 20020022 c
  //   1600fffb 20080001 40880000 8fa80000 23bd0004 40880800 8fa20000 23bd0004 8fa40000 23bd0004 8fb10000
  //   23bd0004 8fb00000 23bd0004 8fa90000 23bd0004 8fa80000 23bd0004 42000018 20160003 20140006 20150001
  //   168020 108100 2149825 132020 20020022 c 1600fffa 295a022 1680fff7 2002000a c
  //   总复位信号应将除ROM以外所有存储组件全部清零
  //   寄存器文件
endmodule

module Control (
  input  [5:0] OPCODE,
  input  [5:0] FUNCT,
  input  [31:0] IR,
  output [3:0] ALUOP,
  output MemRead,
  output shift,
  output ALUSrc,
  output Zero_extend,
  output RegDst,
  output Jump,
  output RegWrite,
  output beq,
  output bne,
  output MemWrite,
  output Jal,
  output EpcRead,
  output jr,
  output EpcWE,
  output syscall,
  output bgez,
  output IEWE,
  output lh,
  output eret
);

  wire add, addi, addiu, addu, \and , andi, comparator_1_eq, comparator_16_eq, comparator_19_eq,
       comparator_20_eq, comparator_21_eq, comparator_22_eq, comparator_23_eq, comparator_24_eq,
       comparator_25_eq, comparator_26_eq, comparator_27_eq, comparator_28_eq, comparator_29_eq,
       comparator_30_eq, comparator_31_eq, comparator_32_eq, comparator_33_eq, EPC, IE, j, lw, mfc, mtc,
       \nor , not_3_out, oppc0, \or , or_1_out, or_2_out, or_3_out, or_4_out, or_10_out, ori, sll, slt, slti,
       sltu, sra, srl, sub, subu, xori;

  Comparator #(.width(6)) comparator_1 (.a(OPCODE), .b({6{1'b0}}), .eq(comparator_1_eq));  // open: gt, lt
  Comparator #(.width(6)) comparator_2 (.a(OPCODE), .b(6'b001000), .eq(addi));  // open: gt, lt
  Comparator #(.width(6)) comparator_3 (.a(OPCODE), .b(6'b001001), .eq(addiu));  // open: gt, lt
  Comparator #(.width(6)) comparator_4 (.a(OPCODE), .b(6'b001100), .eq(andi));  // open: gt, lt
  Comparator #(.width(6)) comparator_5 (.a(OPCODE), .b(6'b001101), .eq(ori));  // open: gt, lt
  Comparator #(.width(6)) comparator_6 (.a(OPCODE), .b(6'b100011), .eq(lw));  // open: gt, lt
  Comparator #(.width(6)) comparator_7 (.a(OPCODE), .b(6'b101011), .eq(MemWrite));  // open: gt, lt
  Comparator #(.width(6)) comparator_8 (.a(OPCODE), .b(6'b000100), .eq(beq));  // open: gt, lt
  Comparator #(.width(6)) comparator_9 (.a(OPCODE), .b(6'b000101), .eq(bne));  // open: gt, lt
  Comparator #(.width(6)) comparator_10 (.a(OPCODE), .b(6'b001010), .eq(slti));  // open: gt, lt
  Comparator #(.width(6)) comparator_11 (.a(OPCODE), .b(6'b000010), .eq(j));  // open: gt, lt
  Comparator #(.width(6)) comparator_12 (.a(OPCODE), .b(6'b000011), .eq(Jal));  // open: gt, lt
  Comparator #(.width(6)) comparator_13 (.a(OPCODE), .b(6'b001110), .eq(xori));  // open: gt, lt
  Comparator #(.width(6)) comparator_14 (.a(OPCODE), .b(6'b100001), .eq(lh));  // open: gt, lt
  Comparator #(.width(6)) comparator_15 (.a(OPCODE), .b(6'b000001), .eq(bgez));  // open: gt, lt
  Comparator #(.width(6)) comparator_16 (.a(OPCODE), .b(6'b010000), .eq(comparator_16_eq));  // open: gt, lt
  Comparator #(.width(5), .mode("unsigned")) comparator_17 (.a({5{1'b0}}), .b(IR[25:21]), .eq(mfc));  // open: gt, lt
  Comparator #(.width(5), .mode("unsigned")) comparator_18 (.a(IR[15:11]), .b({5{1'b0}}), .eq(IE));  // open: gt, lt
  Comparator #(.width(6)) comparator_19 (.a(FUNCT), .b(6'b100000), .eq(comparator_19_eq));  // open: gt, lt
  Comparator #(.width(6)) comparator_20 (.a(FUNCT), .b(6'b100001), .eq(comparator_20_eq));  // open: gt, lt
  Comparator #(.width(6)) comparator_21 (.a(FUNCT), .b(6'b100100), .eq(comparator_21_eq));  // open: gt, lt
  Comparator #(.width(6)) comparator_22 (.a(FUNCT), .b({6{1'b0}}), .eq(comparator_22_eq));  // open: gt, lt
  Comparator #(.width(6)) comparator_23 (.a(FUNCT), .b(6'b000011), .eq(comparator_23_eq));  // open: gt, lt
  Comparator #(.width(6)) comparator_24 (.a(FUNCT), .b(6'b000010), .eq(comparator_24_eq));  // open: gt, lt
  Comparator #(.width(6)) comparator_25 (.a(FUNCT), .b(6'b100010), .eq(comparator_25_eq));  // open: gt, lt
  Comparator #(.width(6)) comparator_26 (.a(FUNCT), .b(6'b100101), .eq(comparator_26_eq));  // open: gt, lt
  Comparator #(.width(6)) comparator_27 (.a(FUNCT), .b(6'b100111), .eq(comparator_27_eq));  // open: gt, lt
  Comparator #(.width(6)) comparator_28 (.a(FUNCT), .b(6'b101010), .eq(comparator_28_eq));  // open: gt, lt
  Comparator #(.width(6)) comparator_29 (.a(FUNCT), .b(6'b101011), .eq(comparator_29_eq));  // open: gt, lt
  Comparator #(.width(6)) comparator_30 (.a(FUNCT), .b(6'b001000), .eq(comparator_30_eq));  // open: gt, lt
  Comparator #(.width(6)) comparator_31 (.a(FUNCT), .b(6'b001100), .eq(comparator_31_eq));  // open: gt, lt
  Comparator #(.width(6)) comparator_32 (.a(FUNCT), .b(6'b100011), .eq(comparator_32_eq));  // open: gt, lt
  Comparator #(.width(6)) comparator_33 (.a(FUNCT), .b(6'b011000), .eq(comparator_33_eq));  // open: gt, lt
  not not_1 (mtc, mfc);
  not not_2 (EPC, IE);
  and and_1 (add, comparator_1_eq, comparator_19_eq);
  and and_2 (addu, comparator_1_eq, comparator_20_eq);
  and and_3 (\and , comparator_1_eq, comparator_21_eq);
  and and_4 (sll, comparator_1_eq, comparator_22_eq);
  and and_5 (sra, comparator_1_eq, comparator_23_eq);
  and and_6 (srl, comparator_1_eq, comparator_24_eq);
  and and_7 (sub, comparator_1_eq, comparator_25_eq);
  and and_8 (\or , comparator_1_eq, comparator_26_eq);
  and and_9 (\nor , comparator_1_eq, comparator_27_eq);
  and and_10 (slt, comparator_1_eq, comparator_28_eq);
  and and_11 (sltu, comparator_1_eq, comparator_29_eq);
  and and_12 (jr, comparator_1_eq, comparator_30_eq);
  and and_13 (syscall, comparator_1_eq, comparator_31_eq);
  and and_14 (subu, comparator_1_eq, comparator_32_eq);
  not not_3 (not_3_out, comparator_33_eq);
  and and_15 (eret, comparator_33_eq, comparator_16_eq);
  and and_16 (oppc0, comparator_16_eq, not_3_out);
  or or_1 (or_1_out, sub, subu);
  or or_2 (or_2_out, \and , andi);
  or or_3 (or_3_out, \or , ori);
  or or_4 (or_4_out, slt, slti);
  or or_5 (MemRead, lw, lh);
  or or_6 (shift, sll, sra, srl);
  or or_7 (Zero_extend, xori, andi, ori);
  or or_8 (RegDst, add, \nor , addu, \and , sll, sra, srl, \or , slt, sltu, subu, sub);
  or or_9 (Jump, j, Jal);
  or or_10 (or_10_out, add, addi, addiu, addu, lw, MemWrite, beq, bne, bgez, lh);
  Priority_Encoder #(.select(4)) priority_encoder_1 (
    .in0(sll), .in1(sra), .in2(srl), .in3(1'b0), .in4(1'b0), .in5(or_10_out), .in6(or_1_out), .in7(or_2_out),
    .in8(or_3_out), .in9(xori), .in10(\nor ), .in11(or_4_out), .in12(sltu), .in13(1'b0), .in14(1'b0),
    .in15(1'b0), .out(ALUOP));  // open: gs, en_out, en_in
  or or_11 (ALUSrc, addi, addiu, andi, sll, sra, srl, ori, lw, MemWrite, slti, xori, lh);
  or or_12 (RegWrite, lh, slt, add, addiu, addu, \and , sll, sra, \nor , srl, \or , sltu, subu, sub, addi, andi, ori, lw, slti, xori, Jal, EpcRead);
  and and_17 (EpcRead, mfc, oppc0, EPC);
  and and_18 (EpcWE, mtc, oppc0, EPC);
  and and_19 (IEWE, mtc, oppc0, IE);

  // Other names for the same wires on the sheet: sw = MemWrite
endmodule

module Decoder (
  input  [31:0] CODE,
  input  shift,
  input  syscall,
  input  RegDst,
  input  Jal,
  input  Zero_extend,
  output [27:0] PCjump,
  output [5:0] OPCODE,
  output [5:0] FUNCT,
  output [4:0] RA,
  output [4:0] RB,
  output [4:0] RW,
  output [31:0] extend
);

  wire [4:0] multiplexer_1_out, multiplexer_2_out;
  wire [31:0] bit_extender_1_out, bit_extender_2_out, bit_extender_3_out, multiplexer_6_out;

  Shifter #(.width(28)) shifter_1 (.in(CODE[27:0]), .\dist (5'b00010), .out(PCjump));
  Multiplexer #(.width(5), .enable("false")) multiplexer_1 (
    .in0(CODE[25:21]), .in1(CODE[20:16]), .out(multiplexer_1_out), .sel(shift));
  Multiplexer #(.width(5), .enable("false")) multiplexer_2 (
    .in0(CODE[20:16]), .in1(CODE[15:11]), .out(multiplexer_2_out), .sel(RegDst));
  Multiplexer #(.width(5), .enable("false")) multiplexer_3 (
    .in0(multiplexer_1_out), .in1(5'b00010), .out(RA), .sel(syscall));
  Multiplexer #(.width(5), .enable("false")) multiplexer_4 (
    .in0(multiplexer_2_out), .in1({5{1'b1}}), .out(RW), .sel(Jal));
  assign bit_extender_1_out = {{16{CODE[15]}}, CODE[15:0]};  // Bit_Extender bit_extender_1
  assign bit_extender_2_out = {{16{1'b0}}, CODE[15:0]};  // Bit_Extender bit_extender_2
  assign bit_extender_3_out = {{27{1'b0}}, CODE[10:6]};  // Bit_Extender bit_extender_3
  Multiplexer #(.width(5), .enable("false")) multiplexer_5 (.in0(CODE[20:16]), .in1(5'b00100), .out(RB), .sel(syscall));
  Multiplexer #(.width(32), .enable("false")) multiplexer_6 (
    .in0(bit_extender_1_out), .in1(bit_extender_2_out), .out(multiplexer_6_out), .sel(Zero_extend));
  Multiplexer #(.width(32), .enable("false")) multiplexer_7 (
    .in0(multiplexer_6_out), .in1(bit_extender_3_out), .out(extend), .sel(shift));

  assign FUNCT = CODE[5:0];
  assign OPCODE = CODE[31:26];
endmodule

// NPC
module Npc (
  input  jr,
  input  [31:0] dA,
  input  [27:0] PCjmp,
  input  jump,
  input  bgez,
  input  bne,
  input  equal,
  input  beq,
  input  [31:0] PC,
  input  [31:0] extendIMM,
  output [31:0] NextPc,
  output [31:0] PCjar
);

  wire and_1_out, and_2_out, and_3_out, cmp, comparator_1_gt, or_1_out;
  wire [31:0] adder_2_out, multiplexer_2_out, multiplexer_3_out, shifter_1_out;

  Adder #(.width(32)) adder_1 (.a(32'h4), .b(PC), .out(PCjar));  // open: cin, cout
  Multiplexer #(.width(32), .enable("false")) multiplexer_1 (.in0(multiplexer_2_out), .in1(dA), .out(NextPc), .sel(jr));
  Shifter #(.width(32)) shifter_1 (.in(extendIMM), .\dist (5'b00010), .out(shifter_1_out));
  not not_1 (cmp, comparator_1_gt);
  Comparator #(.width(32)) comparator_1 (.a({32{1'b0}}), .b(dA), .gt(comparator_1_gt));  // open: eq, lt
  Adder #(.width(32)) adder_2 (.a(PCjar), .b(shifter_1_out), .out(adder_2_out));  // open: cin, cout
  Multiplexer #(.width(32), .enable("false")) multiplexer_2 (
    .in0(multiplexer_3_out), .in1({PCjar[31:28], PCjmp}), .out(multiplexer_2_out), .sel(jump));
  and and_1 (and_1_out, bgez, cmp);
  Multiplexer #(.width(32), .enable("false")) multiplexer_3 (
    .in0(PCjar), .in1(adder_2_out), .out(multiplexer_3_out), .sel(or_1_out));
  or or_1 (or_1_out, and_1_out, and_2_out, and_3_out);
  and and_2 (and_2_out, bne, ~equal);  // AND_Gate
  and and_3 (and_3_out, equal, beq);
endmodule

// IR
module Interrupt (
  input  clk,
  input  ERET,
  input  [31:0] epc_w_v,
  input  IR1,
  input  [31:0] cur_pc,
  input  epc_w_en,
  input  IR2,
  input  IR3,
  input  IEW,
  input  [31:0] IE_V,
  output [31:0] epc,
  output led1,
  output [31:0] next_pc,
  output led2,
  output led3
);

  wire and_1_out, and_2_out, and_3_out, and_4_out, comparator_1_eq, d_ff_1_q, d_ff_2_q, d_ff_3_q, d_ff_7_q,
       hasIR, IE, IR1_t, IR1rst, IR2_t, IR2rst, IR3_t, IR3rst, multiplexer_1_out, not_1_out, not_2_out,
       or_4_out, or_5_out, or_6_out, or_7_out, or_8_out, or_9_out;
  wire [1:0] CurIR, IRp, IRpp, multiplexer_4_out, multiplexer_7_out, multiplexer_8_out,
       priority_encoder_1_out;
  wire [31:0] IRpc, multiplexer_3_out, multiplexer_5_out;

  or or_1 (led1, IR1_t, d_ff_1_q);
  or or_2 (led2, IR2_t, d_ff_2_q);
  or or_3 (led3, IR3_t, d_ff_3_q);
  D_Flip_Flop d_ff_1 (.clk(IR1), .D(1'b1), .Q(d_ff_1_q), .reset(IR1_t));  // open: Qn, preset, en
  D_Flip_Flop d_ff_2 (.clk(IR2), .D(1'b1), .Q(d_ff_2_q), .reset(IR2_t));  // open: Qn, preset, en
  D_Flip_Flop d_ff_3 (.clk(IR3), .D(1'b1), .Q(d_ff_3_q), .reset(IR3_t));  // open: Qn, preset, en
  or or_4 (or_4_out, d_ff_7_q, hasIR);
  Multiplexer #(.disabled(0), .enable("false")) multiplexer_1 (
    .in0(or_4_out), .in1(IE_V[0]), .out(multiplexer_1_out), .sel(IEW));
  or or_5 (or_5_out, d_ff_1_q, IR1_t);
  and and_1 (and_1_out, or_5_out, ~IR1rst);  // AND_Gate
  or or_6 (or_6_out, d_ff_2_q, IR2_t);
  and and_2 (and_2_out, or_6_out, ~IR2rst);  // AND_Gate
  or or_7 (or_7_out, d_ff_3_q, IR3_t);
  and and_3 (and_3_out, or_7_out, ~IR3rst);  // AND_Gate
  and and_4 (and_4_out, multiplexer_1_out, not_1_out);
  not not_1 (not_1_out, ERET);
  D_Flip_Flop d_ff_4 (.clk(clk), .D(and_1_out), .Q(IR1_t));  // open: Qn, preset, en, reset
  D_Flip_Flop d_ff_5 (.clk(clk), .D(and_2_out), .Q(IR2_t));  // open: Qn, preset, en, reset
  D_Flip_Flop d_ff_6 (.clk(clk), .D(and_3_out), .Q(IR3_t));  // open: Qn, preset, en, reset
  D_Flip_Flop d_ff_7 (.clk(clk), .D(and_4_out), .Q(d_ff_7_q), .Qn(IE));  // open: preset, en, reset
  Priority_Encoder #(.select(2), .disabled(0)) priority_encoder_1 (
    .in0(1'b0), .in1(IR1_t), .in2(IR2_t), .in3(IR3_t), .out(priority_encoder_1_out));  // open: gs, en_out, en_in
  Multiplexer #(.select(2), .width(32), .disabled(0), .enable("false")) multiplexer_2 (
    .in1(32'h18), .in2(32'hc0), .in3(32'h168), .out(IRpc), .sel(priority_encoder_1_out));  // open: in0
  Multiplexer #(.width(32), .disabled(0), .enable("false")) multiplexer_3 (
    .in0(cur_pc), .in1(epc_w_v), .out(multiplexer_3_out), .sel(epc_w_en));
  or or_8 (or_8_out, epc_w_en, hasIR);
  Comparator #(.width(2), .mode("unsigned")) comparator_1 (
    .a(priority_encoder_1_out), .b(CurIR), .eq(comparator_1_eq));  // open: gt, lt
  Pull_Resistor pull_resistor_1 (.node(priority_encoder_1_out));
  Decoder_part #(.select(2), .disabled(0)) decoder_1 (
    .out1(IR1rst), .out2(IR2rst), .out3(IR3rst), .sel(priority_encoder_1_out), .en(ERET));  // open: out0
  Multiplexer #(.width(2), .disabled(0), .enable("false")) multiplexer_4 (
    .in0(priority_encoder_1_out), .in1(IRp), .out(multiplexer_4_out), .sel(ERET));
  or or_9 (or_9_out, hasIR, ERET);
  Register #(.width(32)) u_EPC (.D(multiplexer_3_out), .en(or_8_out), .Q(epc), .clk(clk));  // open: clr
  Multiplexer #(.width(32), .disabled(0), .enable("false")) multiplexer_5 (
    .in0(cur_pc), .in1(IRpc), .out(multiplexer_5_out), .sel(hasIR));
  not not_2 (not_2_out, comparator_1_eq);
  and and_5 (hasIR, not_2_out, IE);
  Register #(.width(2)) u_CurIR (.D(multiplexer_4_out), .en(or_9_out), .Q(CurIR), .clk(clk));  // open: clr
  Multiplexer #(.width(32), .disabled(0), .enable("false")) multiplexer_6 (
    .in0(multiplexer_5_out), .in1(epc), .out(next_pc), .sel(ERET));
  Multiplexer #(.width(2), .disabled(0), .enable("false")) multiplexer_7 (
    .in0(CurIR), .in1(IRpp), .out(multiplexer_7_out), .sel(ERET));
  Register #(.width(2)) CurIR_2 (.D(multiplexer_7_out), .en(or_9_out), .Q(IRp), .clk(clk));  // open: clr
  Multiplexer #(.width(2), .disabled(0), .enable("false")) multiplexer_8 (
    .in0(IRp), .in1(2'b00), .out(multiplexer_8_out), .sel(ERET));
  Register #(.width(2)) CurIR_3 (.D(multiplexer_8_out), .en(or_9_out), .Q(IRpp), .clk(clk));  // open: clr
endmodule
