// Logisim project 气泡流水线.circ as structural Verilog: 14 circuits, main circuit cpu
module cpu (
);

  wire alu_1_equal, and_1_out, and_2_out, and_3_out, bSuc, BubId, BubIf, clk, conti, control_1_alusrc,
       control_1_beq, control_1_bltz, control_1_bne, control_1_jal, control_1_jr, control_1_jump,
       control_1_lh, control_1_memread, control_1_memwrite, control_1_regdst, control_1_regwrite,
       control_1_shift, control_1_syscall, control_1_zero_extend, counter_4_q, ex_mem_1_hault_2,
       ex_mem_1_memread_out, ex_mem_1_memwrite_out, hault, haultSig, id_ex_1_alusrc_2, id_ex_1_beq_out,
       id_ex_1_bltz_2, id_ex_1_bne_out, id_ex_1_hault_2, id_ex_1_jr_out, id_ex_1_jump_out, id_ex_1_lh_out,
       id_ex_1_mem_read_out, id_ex_1_memw_out, JAL, JMP, lh, mem_wb_1_rw_select_2, not_1_out, not_2_out,
       or_1_out, or_2_out, pcEnable, rbValid, RST, rweEX, rweMEM, rweWB, stall, syscall_1_hault, we;
  wire [3:0] control_1_aluop, id_ex_1_aluop_out, multiplexer_2_out, multiplexer_3_out;
  wire [4:0] decoder_1_rw, rA, rB, rW, rWEX, rWMEM, rWWB;
  wire [5:0] decoder_1_funct, decoder_1_opcode;
  wire [15:0] adder_1_out, adder_2_out, adder_4_out, multiplexer_4_out, negator_1_out, shifter_1_out, \单周期数 ,
       \总周期数 , \无条件分支指令数 , \有条件分支成功跳转 , \气泡数 ;
  wire [31:0] alu_1_result, decoder_1_extend, decoder_1_pcjump, ex_mem_1_rb_out, ex_mem_1_result_out,
       id_ex_1_imm_out, id_ex_1_pcjump_out, id_ex_1_ra_out, id_ex_1_rb_out, if_id_1_ir_out, if_id_1_npc_out,
       mem_wb_1_alu_result_2, mem_wb_1_mem_value_2, mips_ram_1_p9, multiplexer_1_out, multiplexer_5_out,
       multiplexer_6_out, multiplexer_9_out, npc_1_nextpc, PC, pcEX, pcEX_4, predictpc_1_pc_out,
       pull_resistor_2_node, register_1_ra_2, register_1_rb_2, rom_1_data, syso;

  Button \u_总复位  (.out(RST));
  Hex_Digit_Display hex_digit_display_1 (.value(syso[31:28]));  // open: dp
  Hex_Digit_Display hex_digit_display_2 (.value(syso[27:24]));  // open: dp
  Register_part #(.width(32)) u_pc (.D(predictpc_1_pc_out), .en(pcEnable), .Q(PC), .clk(clk), .clr(RST));
  Hex_Digit_Display hex_digit_display_3 (.value(syso[19:16]));  // open: dp
  Hex_Digit_Display hex_digit_display_4 (.value(syso[23:20]));  // open: dp
  and and_1 (and_1_out, JMP, pcEnable);
  and and_2 (and_2_out, bSuc, pcEnable);
  and and_3 (and_3_out, hault, stall);
  Hex_Digit_Display hex_digit_display_5 (.value(syso[15:12]));  // open: dp
  Hex_Digit_Display hex_digit_display_6 (.value(syso[11:8]));  // open: dp
  ROM #(.addrWidth(10), .dataWidth(32)) rom_1 (.addr(PC[11:2]), .data(rom_1_data));  // open: sel
  PredictPC predictpc_1 (.pc(PC), .next_pc(npc_1_nextpc), .pc_out(predictpc_1_pc_out), .JMP(JMP), .bSucces(bSuc));
  Counter #(.width(16), .max('hffff)) counter_1 (
    .count(and_1_out), .Q(\无条件分支指令数 ), .clk(clk), .clr(RST));  // open: load, D, carry
  Counter #(.width(16), .max('hffff)) counter_2 (
    .count(and_2_out), .Q(\有条件分支成功跳转 ), .clk(clk), .clr(RST));  // open: load, D, carry
  Counter #(.width(16), .max('hffff)) counter_3 (
    .count(and_3_out), .Q(\气泡数 ), .clk(clk), .clr(RST));  // open: load, D, carry
  Hex_Digit_Display hex_digit_display_7 (.value(syso[3:0]));  // open: dp
  Hex_Digit_Display hex_digit_display_8 (.value(syso[7:4]));  // open: dp
  Clock clock_1 (.out(clk));
  Button Continue (.out(conti));
  IF_ID if_id_1 (
    .NPC_in(PC), .IR_in(rom_1_data), .NPC_out(if_id_1_npc_out), .IR_out(if_id_1_ir_out), .clk(clk),
    .rst(BubIf), .enable(pcEnable));
  Decoder decoder_1 (
    .CODE(if_id_1_ir_out), .PCjump(decoder_1_pcjump), .OPCODE(decoder_1_opcode), .FUNCT(decoder_1_funct),
    .rA(rA), .rB(rB), .shift(control_1_shift), .syscall(control_1_syscall),
    .Zero_extend(control_1_zero_extend), .extend(decoder_1_extend), .rW(decoder_1_rw),
    .RegDst(control_1_regdst), .Jal(control_1_jal));
  Register register_1 (
    .w(multiplexer_6_out), .clk(not_1_out), .we(we), .rw(rW), .ra(rA), .rb(rB), .RA_2(register_1_ra_2),
    .RB_2(register_1_rb_2));
  not not_1 (not_1_out, clk);
  // Probe on \总周期数 
  // Probe on \无条件分支指令数 
  // Probe on \有条件分支成功跳转 
  // Probe on \气泡数 
  Control control_1 (
    .ALUOP(control_1_aluop), .shift(control_1_shift), .Zero_extend(control_1_zero_extend),
    .ALUSrc(control_1_alusrc), .RegDst(control_1_regdst), .RegWrite(control_1_regwrite),
    .Jump(control_1_jump), .beq(control_1_beq), .bne(control_1_bne), .MemWrite(control_1_memwrite),
    .Jal(control_1_jal), .jr(control_1_jr), .syscall(control_1_syscall), .bltz(control_1_bltz),
    .OPCODE(decoder_1_opcode), .FUNCT(decoder_1_funct), .lh(control_1_lh), .memread(control_1_memread),
    .rbValid(rbValid));
  syscall syscall_1 (
    .RA(register_1_ra_2), .syscall(control_1_syscall), .syscall_out(syso), .hault(syscall_1_hault),
    .RB(register_1_rb_2), .clk(clk), .rst(RST));
  Counter #(.width(1), .max('h1)) counter_4 (
    .count(haultSig), .Q(counter_4_q), .clk(clk), .clr(or_1_out));  // open: load, D, carry
  or or_1 (or_1_out, conti, RST);
  ID_EX id_ex_1 (
    .jump(control_1_jump), .beq(control_1_beq), .bne(control_1_bne), .memw(control_1_memwrite),
    .PC(if_id_1_npc_out), .aluop(control_1_aluop), .jr(control_1_jr), .alusrc(control_1_alusrc),
    .bltz(control_1_bltz), .IR_in(if_id_1_ir_out), .rw_enable(control_1_regwrite), .lh(control_1_lh),
    .jump_out(id_ex_1_jump_out), .beq_out(id_ex_1_beq_out), .bne_out(id_ex_1_bne_out),
    .memw_out(id_ex_1_memw_out), .PC_2(pcEX), .aluop_out(id_ex_1_aluop_out), .jr_out(id_ex_1_jr_out),
    .alusrc_2(id_ex_1_alusrc_2), .bltz_2(id_ex_1_bltz_2), .rw_enable_2(rweEX), .lh_out(id_ex_1_lh_out),
    .clk(clk), .rst(BubId), .imm(decoder_1_extend), .imm_out(id_ex_1_imm_out), .pcjump(decoder_1_pcjump),
    .pcjump_out(id_ex_1_pcjump_out), .RA(register_1_ra_2), .RA_out(id_ex_1_ra_out), .RB(register_1_rb_2),
    .RB_out(id_ex_1_rb_out), .memread(control_1_memread), .mem_read_out(id_ex_1_mem_read_out),
    .rW(decoder_1_rw), .rW_out(rWEX), .hault(syscall_1_hault), .hault_2(id_ex_1_hault_2),
    .jal(control_1_jal), .jal_2(JAL));  // open: IR_out, enable
  not not_2 (not_2_out, stall);
  not not_3 (hault, counter_4_q);
  // Probe on \单周期数 
  Multiplexer #(.width(32), .enable("false")) multiplexer_1 (
    .in0(id_ex_1_rb_out), .in1(id_ex_1_imm_out), .out(multiplexer_1_out), .sel(id_ex_1_alusrc_2));
  and and_4 (pcEnable, not_2_out, hault);
  Counter #(.width(16), .max('hffff)) counter_5 (
    .count(hault), .Q(\总周期数 ), .clk(clk), .clr(RST));  // open: load, D, carry
  Npc npc_1 (
    .PCjmp(id_ex_1_pcjump_out), .extendIMM(id_ex_1_imm_out), .bne(id_ex_1_bne_out), .beq(id_ex_1_beq_out),
    .PC(pcEX), .jr(id_ex_1_jr_out), .dA(id_ex_1_ra_out), .equal(alu_1_equal), .NextPc(npc_1_nextpc),
    .bltz(id_ex_1_bltz_2), .jump(id_ex_1_jump_out), .JMP(JMP), .bSuccess(bSuc));
  ALU alu_1 (
    .X(id_ex_1_ra_out), .Y(multiplexer_1_out), .Result(alu_1_result), .ALUOP(id_ex_1_aluop_out),
    .equal(alu_1_equal));
  Adder #(.width(16)) adder_1 (.a(\无条件分支指令数 ), .b(\有条件分支成功跳转 ), .out(adder_1_out));  // open: cin, cout
  EX_MEM ex_mem_1 (
    .result(alu_1_result), .result_out(ex_mem_1_result_out), .clk(clk), .rst(RST),
    .memread(id_ex_1_mem_read_out), .memread_out(ex_mem_1_memread_out), .rW(rWEX), .rW_out(rWMEM),
    .memwrite(id_ex_1_memw_out), .memwrite_out(ex_mem_1_memwrite_out), .lh(id_ex_1_lh_out), .lh_out(lh),
    .rw_enable(rweEX), .rw_enable_2(rweMEM), .RB(id_ex_1_rb_out), .RB_out(ex_mem_1_rb_out),
    .hault(id_ex_1_hault_2), .hault_2(ex_mem_1_hault_2));  // open: NPC_in, NPC_out, IR_in, IR_out
  Adder #(.width(16)) adder_2 (.a(\气泡数 ), .b(shifter_1_out), .out(adder_2_out));  // open: cin, cout
  Shifter #(.width(16)) shifter_1 (.in(adder_1_out), .\dist (4'b0001), .out(shifter_1_out));
  Multiplexer #(.width(4), .enable("false")) multiplexer_2 (
    .in0(4'b0011), .in1(4'b1100), .out(multiplexer_2_out), .sel(ex_mem_1_result_out[1]));
  or or_2 (or_2_out, JMP, bSuc);
  Bubble bubble_1 (
    .rA(rA), .rB(rB), .rWEX(rWEX), .rWMEM(rWMEM), .rweEX(rweEX), .rweMEM(rweMEM), .JMP(or_2_out),
    .BubId(BubId), .BubIf(BubIf), .stall(stall), .rBvalid(rbValid));
  Adder #(.width(32)) adder_3 (.a(pcEX), .b(32'h4), .out(pcEX_4));  // open: cin, cout
  Negator #(.width(16)) negator_1 (.in(adder_2_out), .out(negator_1_out));
  Multiplexer #(.width(4), .enable("false")) multiplexer_3 (
    .in0(4'b1111), .in1(multiplexer_2_out), .out(multiplexer_3_out), .sel(lh));
  Adder #(.width(16)) adder_4 (.a(\总周期数 ), .b(negator_1_out), .out(adder_4_out));  // open: cin, cout
  // MIPS_RAM mips_ram_1: pin names not known; wires that end beside it: RST, ex_mem_1_result_out, ex_mem_1_result_out[21:2], ex_mem_1_rb_out, ex_mem_1_memwrite_out, multiplexer_3_out, clk, RST, mips_ram_1_p9
  Multiplexer #(.width(16), .enable("false")) multiplexer_4 (
    .in0(mips_ram_1_p9[15:0]), .in1(mips_ram_1_p9[31:16]), .out(multiplexer_4_out),
    .sel(ex_mem_1_result_out[1]));
  Adder #(.width(16)) adder_5 (.a(adder_4_out), .b(16'hfffc), .out(\单周期数 ));  // open: cin, cout
  Pull_Resistor pull_resistor_1 (.node(mips_ram_1_p9));
  Pull_Resistor pull_resistor_2 (.node(pull_resistor_2_node));
  assign pull_resistor_2_node = {{16{multiplexer_4_out[15]}}, multiplexer_4_out};  // Bit_Extender bit_extender_1
  MEM_WB mem_wb_1 (
    .alu_result(ex_mem_1_result_out), .alu_result_2(mem_wb_1_alu_result_2), .mem_value(multiplexer_5_out),
    .mem_value_2(mem_wb_1_mem_value_2), .clk(clk), .rW(rWMEM), .rW_out(rWWB), .rw_enable(rweMEM),
    .rw_enable_2(rweWB), .rw_select(ex_mem_1_memread_out), .rw_select_2(mem_wb_1_rw_select_2),
    .hault(ex_mem_1_hault_2), .hault_2(haultSig));  // open: rst
  Multiplexer #(.width(32), .enable("false")) multiplexer_5 (
    .in0(mips_ram_1_p9), .in1(pull_resistor_2_node), .out(multiplexer_5_out), .sel(lh));
  Multiplexer #(.width(32), .enable("false")) multiplexer_6 (
    .in0(multiplexer_9_out), .in1(pcEX_4), .out(multiplexer_6_out), .sel(JAL));
  Multiplexer #(.enable("false")) multiplexer_7 (.in0(rweWB), .in1(1'b1), .out(we), .sel(JAL));
  Multiplexer #(.width(5), .enable("false")) multiplexer_8 (.in0(rWWB), .in1({5{1'b1}}), .out(rW), .sel(JAL));
  Multiplexer #(.width(32), .enable("false")) multiplexer_9 (
    .in0(mem_wb_1_alu_result_2), .in1(mem_wb_1_mem_value_2), .out(multiplexer_9_out),
    .sel(mem_wb_1_rw_select_2));

  // Notes on the sheet:
  //   数码管输出应该用寄存器锁存，否则显示数据只能一闪而过
  //   可以通过项目增加Logisim库的方式将前几次实验完成的电路作为子电路引入到本电路中使用
  //   指令存储器
  //   contents of rom_1 (hex, n*v repeats v):
  //   20110001 8000005 20110001 20120002 20130003 8000009 20110001 20120002 20130003 800000d 20110001
  //   20120002 20130003 8000011 20110001 20120002 20130003 c0000b8 20100001 20110001 118fc0 112020
  //   20020022 c 118882 12200001 8000015 112020 20020022 c 20110001 118880 112020 20020022 c 12200001
  //   800001f 20110001 118fc0 112020 20020022 c 1188c3 112020 20020022 c 118903 112020 20020022 c 118903
  //   112020 20020022 c 118903 112020 20020022 c 118903 112020 20020022 c 118903 112020 20020022 c 118903
  //   112020 20020022 c 118903 112020 20020022 c 20100001 109fc0 139fc3 8021 2012000c 24160003 26100001
  //   3210000f 20080008 20090001 139900 2709825 132020 20020022 c 1094022 1500fff9 22100001 2018000f
  //   2188024 108700 20080008 20090001 139902 2709825 132021 20020022 c 1094022 1500fff9 108702 2c9b022
  //   12c00001 8000050 4020 1084027 84400 3508ffff 82021 20020022 c 2010ffff 20110000 ae300000 22100001
  //   22310004 ae300000 22100001 22310004 ae300000 22100001 22310004 ae300000 22100001 22310004 ae300000
  //   22100001 22310004 ae300000 22100001 22310004 ae300000 22100001 22310004 ae300000 22100001 22310004
  //   ae300000 22100001 22310004 ae300000 22100001 22310004 ae300000 22100001 22310004 ae300000 22100001
  //   22310004 ae300000 22100001 22310004 ae300000 22100001 22310004 ae300000 22100001 22310004 ae300000
  //   22100001 22310004 22100001 8020 2011003c 8e130000 8e340000 274402a 11000002 ae330000 ae140000
  //   2231fffc 1611fff8 102020 20020022 c 22100004 2011003c 1611fff2 2002000a c 20100000 22100001 102020
  //   20020022 c 22100002 102020 20020022 c 22100003 102020 20020022 c 22100004 102020 20020022 c 22100005
  //   102020 20020022 c 22100006 102020 20020022 c 22100007 102020 20020022 c 22100008 102020 20020022
  //   20020022 c 3e00008
  //   数码管输出
  //   总复位信号应将除ROM以外所有存储组件全部清零
endmodule

module Control (
  input  [5:0] OPCODE,
  input  [5:0] FUNCT,
  output [3:0] ALUOP,
  output shift,
  output ALUSrc,
  output Zero_extend,
  output RegDst,
  output Jump,
  output RegWrite,
  output beq,
  output bne,
  output MemWrite,
  output Jal,
  output jr,
  output syscall,
  output bltz,
  output memread,
  output lh,
  output rbValid
);

  wire add, addi, addiu, addu, \and , andi, comparator_1_eq, comparator_17_eq, comparator_18_eq,
       comparator_19_eq, comparator_20_eq, comparator_21_eq, comparator_22_eq, comparator_23_eq,
       comparator_24_eq, comparator_25_eq, comparator_26_eq, comparator_27_eq, comparator_28_eq,
       comparator_29_eq, j, lw, \nor , \or , or_1_out, or_2_out, or_3_out, or_4_out, or_9_out, ori, sll, slt,
       slti, sltiu, sltu, sra, srl, sub, xori;

  Comparator #(.width(6)) comparator_1 (.a(OPCODE), .b({6{1'b0}}), .eq(comparator_1_eq));  // open: gt, lt
  Comparator #(.width(6)) comparator_2 (.a(OPCODE), .b(6'b001000), .eq(addi));  // open: gt, lt
  Comparator #(.width(6)) comparator_3 (.a(OPCODE), .b(6'b001001), .eq(addiu));  // open: gt, lt
  Comparator #(.width(6)) comparator_4 (.a(OPCODE), .b(6'b001100), .eq(andi));  // open: gt, lt
  Comparator #(.width(6)) comparator_5 (.a(OPCODE), .b(6'b001101), .eq(ori));  // open: gt, lt
  Comparator #(.width(6)) comparator_6 (.a(OPCODE), .b(6'b100011), .eq(lw));  // open: gt, lt
  Comparator #(.width(6)) comparator_7 (.a(OPCODE), .b(6'b101011), .eq(MemWrite));  // open: gt, lt
  Comparator #(.width(6)) comparator_8 (.a(OPCODE), .b(6'b000100), .eq(beq));  // open: gt, lt
  Comparator #(.width(6)) comparator_9 (.a(OPCODE), .b(6'b000101), .eq(bne));  // open: gt, lt
  Comparator #(.width(6)) comparator_10 (.a(OPCODE), .b(6'b001010), .eq(slti));  // open: gt, lt
  Comparator #(.width(6)) comparator_11 (.a(OPCODE), .b(6'b000010), .eq(j));  // open: gt, lt
  Comparator #(.width(6)) comparator_12 (.a(OPCODE), .b(6'b000011), .eq(Jal));  // open: gt, lt
  Comparator #(.width(6)) comparator_13 (.a(OPCODE), .b(6'b001110), .eq(xori));  // open: gt, lt
  Comparator #(.width(6)) comparator_14 (.a(OPCODE), .b(6'b100001), .eq(lh));  // open: gt, lt
  Comparator #(.width(6)) comparator_15 (.a(OPCODE), .b(6'b000001), .eq(bltz));  // open: gt, lt
  Comparator #(.width(6)) comparator_16 (.a(OPCODE), .b(6'b001011), .eq(sltiu));  // open: gt, lt
  Comparator #(.width(6)) comparator_17 (.a(FUNCT), .b(6'b100000), .eq(comparator_17_eq));  // open: gt, lt
  Comparator #(.width(6)) comparator_18 (.a(FUNCT), .b(6'b100001), .eq(comparator_18_eq));  // open: gt, lt
  Comparator #(.width(6)) comparator_19 (.a(FUNCT), .b(6'b100100), .eq(comparator_19_eq));  // open: gt, lt
  Comparator #(.width(6)) comparator_20 (.a(FUNCT), .b({6{1'b0}}), .eq(comparator_20_eq));  // open: gt, lt
  Comparator #(.width(6)) comparator_21 (.a(FUNCT), .b(6'b000011), .eq(comparator_21_eq));  // open: gt, lt
  Comparator #(.width(6)) comparator_22 (.a(FUNCT), .b(6'b000010), .eq(comparator_22_eq));  // open: gt, lt
  Comparator #(.width(6)) comparator_23 (.a(FUNCT), .b(6'b100010), .eq(comparator_23_eq));  // open: gt, lt
  Comparator #(.width(6)) comparator_24 (.a(FUNCT), .b(6'b100101), .eq(comparator_24_eq));  // open: gt, lt
  Comparator #(.width(6)) comparator_25 (.a(FUNCT), .b(6'b100111), .eq(comparator_25_eq));  // open: gt, lt
  Comparator #(.width(6)) comparator_26 (.a(FUNCT), .b(6'b101010), .eq(comparator_26_eq));  // open: gt, lt
  Comparator #(.width(6)) comparator_27 (.a(FUNCT), .b(6'b101011), .eq(comparator_27_eq));  // open: gt, lt
  Comparator #(.width(6)) comparator_28 (.a(FUNCT), .b(6'b001000), .eq(comparator_28_eq));  // open: gt, lt
  Comparator #(.width(6)) comparator_29 (.a(FUNCT), .b(6'b001100), .eq(comparator_29_eq));  // open: gt, lt
  and and_1 (add, comparator_1_eq, comparator_17_eq);
  and and_2 (addu, comparator_1_eq, comparator_18_eq);
  and and_3 (\and , comparator_1_eq, comparator_19_eq);
  and and_4 (sll, comparator_1_eq, comparator_20_eq);
  and and_5 (sra, comparator_1_eq, comparator_21_eq);
  and and_6 (srl, comparator_1_eq, comparator_22_eq);
  and and_7 (sub, comparator_1_eq, comparator_23_eq);
  and and_8 (\or , comparator_1_eq, comparator_24_eq);
  and and_9 (\nor , comparator_1_eq, comparator_25_eq);
  and and_10 (slt, comparator_1_eq, comparator_26_eq);
  and and_11 (sltu, comparator_1_eq, comparator_27_eq);
  and and_12 (jr, comparator_1_eq, comparator_28_eq);
  and and_13 (syscall, comparator_1_eq, comparator_29_eq);
  or or_1 (or_1_out, \and , andi);
  or or_2 (or_2_out, \or , ori);
  or or_3 (or_3_out, slt, slti);
  or or_4 (or_4_out, sltu, sltiu);
  or or_5 (shift, sll, sra, srl);
  or or_6 (Zero_extend, xori, andi, ori);
  or or_7 (RegDst, add, \nor , addu, \and , sll, sra, srl, \or , slt, sltu, sub);
  or or_8 (Jump, j, Jal);
  or or_9 (or_9_out, add, addi, addiu, addu, lw, MemWrite, beq, bne, bltz, lh);
  Priority_Encoder #(.select(4)) priority_encoder_1 (
    .in0(sll), .in1(sra), .in2(srl), .in3(1'b0), .in4(1'b0), .in5(or_9_out), .in6(sub), .in7(or_1_out),
    .in8(or_2_out), .in9(xori), .in10(\nor ), .in11(or_3_out), .in12(or_4_out), .in13(1'b0), .in14(1'b0),
    .in15(1'b0), .out(ALUOP));  // open: gs, en_out, en_in
  or or_10 (ALUSrc, addi, addiu, andi, sll, sra, srl, sltiu, ori, lw, MemWrite, slti, xori, lh);
  or or_11 (RegWrite, slt, add, addiu, addu, \and , sll, sra, \nor , srl, \or , lh, sltu, sltiu, sub, addi, andi, ori, lw, slti, xori, sltiu);
  or or_12 (memread, lw, lh);
  or or_13 (rbValid, beq, RegDst, bne, MemWrite);

  // Other names for the same wires on the sheet: sw = MemWrite
endmodule

module Decoder (
  input  [31:0] CODE,
  input  shift,
  input  syscall,
  input  RegDst,
  input  Jal,
  input  Zero_extend,
  output [31:0] PCjump,
  output [5:0] OPCODE,
  output [5:0] FUNCT,
  output [4:0] rA,
  output [4:0] rB,
  output [4:0] rW,
  output [31:0] extend
);

  wire [4:0] multiplexer_1_out, multiplexer_2_out;
  wire [31:0] bit_extender_1_out, bit_extender_2_out, bit_extender_3_out, multiplexer_6_out;

  Shifter #(.width(28)) shifter_1 (.in(CODE[27:0]), .\dist (5'b00010), .out(PCjump[27:0]));
  Multiplexer #(.width(5), .enable("false")) multiplexer_1 (
    .in0(CODE[25:21]), .in1(CODE[20:16]), .out(multiplexer_1_out), .sel(shift));
  Multiplexer #(.width(5), .enable("false")) multiplexer_2 (
    .in0(CODE[20:16]), .in1(CODE[15:11]), .out(multiplexer_2_out), .sel(RegDst));
  Multiplexer #(.width(5), .enable("false")) multiplexer_3 (
    .in0(multiplexer_1_out), .in1(5'b00010), .out(rA), .sel(syscall));
  Multiplexer #(.width(5), .enable("false")) multiplexer_4 (
    .in0(multiplexer_2_out), .in1({5{1'b1}}), .out(rW), .sel(Jal));
  assign bit_extender_1_out = {{16{CODE[15]}}, CODE[15:0]};  // Bit_Extender bit_extender_1
  assign bit_extender_2_out = {{16{1'b0}}, CODE[15:0]};  // Bit_Extender bit_extender_2
  assign bit_extender_3_out = {{27{1'b0}}, CODE[10:6]};  // Bit_Extender bit_extender_3
  Multiplexer #(.width(5), .enable("false")) multiplexer_5 (.in0(CODE[20:16]), .in1(5'b00100), .out(rB), .sel(syscall));
  Multiplexer #(.width(32), .enable("false")) multiplexer_6 (
    .in0(bit_extender_1_out), .in1(bit_extender_2_out), .out(multiplexer_6_out), .sel(Zero_extend));
  Multiplexer #(.width(32), .enable("false")) multiplexer_7 (
    .in0(multiplexer_6_out), .in1(bit_extender_3_out), .out(extend), .sel(shift));

  assign FUNCT = CODE[5:0];
  assign OPCODE = CODE[31:26];
  assign PCjump[31:28] = 4'b0000;

  // Notes on the sheet:
  //   if regDst is false then rb is invalid
endmodule

// NPC
module Npc (
  input  jr,
  input  [31:0] dA,
  input  [31:0] PCjmp,
  input  jump,
  input  bltz,
  input  bne,
  input  equal,
  input  beq,
  input  [31:0] PC,
  input  [31:0] extendIMM,
  output JMP,
  output [31:0] NextPc,
  output bSuccess
);

  wire and_1_out, and_2_out, and_3_out, cmp;
  wire [3:0] adder_1_out_2;
  wire [27:0] adder_1_out;
  wire [31:0] adder_2_out, multiplexer_2_out, multiplexer_3_out, shifter_1_out;

  Adder #(.width(32)) adder_1 (.a(32'h4), .b(PC), .out({adder_1_out_2, adder_1_out}));  // open: cin, cout
  Multiplexer #(.width(32), .enable("false")) multiplexer_1 (.in0(multiplexer_2_out), .in1(dA), .out(NextPc), .sel(jr));
  Shifter #(.width(32)) shifter_1 (.in(extendIMM), .\dist (5'b00010), .out(shifter_1_out));
  Comparator #(.width(32)) comparator_1 (.a({32{1'b0}}), .b(dA), .gt(cmp));  // open: eq, lt
  Adder #(.width(32)) adder_2 (
    .a({adder_1_out_2, adder_1_out}), .b(shifter_1_out), .out(adder_2_out));  // open: cin, cout
  Multiplexer #(.width(32), .enable("false")) multiplexer_2 (
    .in0(multiplexer_3_out), .in1({adder_1_out_2, PCjmp[27:0]}), .out(multiplexer_2_out), .sel(jump));
  and and_1 (and_1_out, bltz, cmp);
  Multiplexer #(.width(32), .enable("false")) multiplexer_3 (
    .in0({adder_1_out_2, adder_1_out}), .in1(adder_2_out), .out(multiplexer_3_out), .sel(bSuccess));
  or or_1 (bSuccess, and_1_out, and_2_out, and_3_out);
  and and_2 (and_2_out, bne, ~equal);  // AND_Gate
  and and_3 (and_3_out, equal, beq);
  or or_2 (JMP, jr, jump);
endmodule

module IF_ID (
  input  enable,
  input  [31:0] NPC_in,
  input  [31:0] IR_in,
  input  rst,
  input  clk,
  output [31:0] NPC_out,
  output [31:0] IR_out
);

  wire [31:0] multiplexer_1_out, multiplexer_2_out;

  Multiplexer #(.width(32), .enable("false")) multiplexer_1 (
    .in0(NPC_in), .in1({32{1'b0}}), .out(multiplexer_1_out), .sel(rst));
  Multiplexer #(.width(32), .enable("false")) multiplexer_2 (
    .in0(IR_in), .in1({32{1'b0}}), .out(multiplexer_2_out), .sel(rst));
  Register_part #(.width(32)) register_1 (.D(multiplexer_1_out), .en(enable), .Q(NPC_out), .clk(clk));  // open: clr
  Register_part #(.width(32)) register_2 (.D(multiplexer_2_out), .en(enable), .Q(IR_out), .clk(clk));  // open: clr
endmodule

// Reg
module Register (
  input  [31:0] w,
  input  clk,
  input  we,
  input  [4:0] rw,
  input  [4:0] ra,
  input  [4:0] rb,
  output [31:0] RA_2,
  output [31:0] RB_2
);

  // RegisterFile registerfile_1: pin names not known; wires that end beside it: w, clk, we, rw, ra, rb, RA_2, RB_2
endmodule

module test (
  input  [31:0] CODE,
  input  RegDst,
  input  Jal,
  output [4:0] RW
);

  wire [4:0] multiplexer_1_out, undriven;

  Multiplexer #(.width(5), .enable("false")) multiplexer_1 (
    .in0(undriven), .in1(CODE[15:11]), .out(multiplexer_1_out), .sel(RegDst));
  Multiplexer #(.width(5), .enable("false")) multiplexer_2 (
    .in0(multiplexer_1_out), .in1({5{1'b1}}), .out(RW), .sel(Jal));
endmodule

module ID_EX (
  input  [31:0] imm,
  input  jal,
  input  hault,
  input  jump,
  input  [31:0] pcjump,
  input  alusrc,
  input  beq,
  input  [31:0] PC,
  input  rw_enable,
  input  bne,
  input  memw,
  input  [31:0] IR_in,
  input  jr,
  input  bltz,
  input  [31:0] RA,
  input  [4:0] rW,
  input  lh,
  input  [31:0] RB,
  input  [3:0] aluop,
  input  memread,
  input  clk,
  input  rst,
  input  enable,
  output [31:0] imm_out,
  output jal_2,
  output hault_2,
  output jump_out,
  output [31:0] pcjump_out,
  output alusrc_2,
  output beq_out,
  output [31:0] PC_2,
  output rw_enable_2,
  output bne_out,
  output memw_out,
  output [31:0] IR_out,
  output jr_out,
  output bltz_2,
  output [31:0] RA_out,
  output [4:0] rW_out,
  output lh_out,
  output [31:0] RB_out,
  output [3:0] aluop_out,
  output mem_read_out
);

  wire multiplexer_7_out, multiplexer_8_out, multiplexer_9_out, multiplexer_10_out, multiplexer_13_out,
       multiplexer_14_out, multiplexer_15_out, multiplexer_16_out, multiplexer_17_out, multiplexer_18_out,
       multiplexer_19_out, multiplexer_20_out;
  wire [3:0] multiplexer_12_out;
  wire [4:0] multiplexer_11_out;
  wire [31:0] multiplexer_1_out, multiplexer_2_out, multiplexer_3_out, multiplexer_4_out, multiplexer_5_out,
       multiplexer_6_out;

  Multiplexer #(.width(32), .enable("false")) multiplexer_1 (
    .in0(imm), .in1({32{1'b0}}), .out(multiplexer_1_out), .sel(rst));
  Multiplexer #(.width(32), .enable("false")) multiplexer_2 (
    .in0(pcjump), .in1({32{1'b0}}), .out(multiplexer_2_out), .sel(rst));
  Multiplexer #(.width(32), .enable("false")) multiplexer_3 (
    .in0(PC), .in1({32{1'b0}}), .out(multiplexer_3_out), .sel(rst));
  Multiplexer #(.width(32), .enable("false")) multiplexer_4 (
    .in0(IR_in), .in1({32{1'b0}}), .out(multiplexer_4_out), .sel(rst));
  Multiplexer #(.width(32), .enable("false")) multiplexer_5 (
    .in0(RA), .in1({32{1'b0}}), .out(multiplexer_5_out), .sel(rst));
  Multiplexer #(.width(32), .enable("false")) multiplexer_6 (
    .in0(RB), .in1({32{1'b0}}), .out(multiplexer_6_out), .sel(rst));
  Register_part #(.width(32)) register_1 (.D(multiplexer_1_out), .en(enable), .Q(imm_out), .clk(clk));  // open: clr
  Register_part #(.width(32)) register_2 (.D(multiplexer_2_out), .en(enable), .Q(pcjump_out), .clk(clk));  // open: clr
  Register_part #(.width(32)) register_3 (.D(multiplexer_3_out), .en(enable), .Q(PC_2), .clk(clk));  // open: clr
  Register_part #(.width(32)) register_4 (.D(multiplexer_4_out), .en(enable), .Q(IR_out), .clk(clk));  // open: clr
  Register_part #(.width(32)) register_5 (.D(multiplexer_5_out), .en(enable), .Q(RA_out), .clk(clk));  // open: clr
  Register_part #(.width(32)) register_6 (.D(multiplexer_6_out), .en(enable), .Q(RB_out), .clk(clk));  // open: clr
  Multiplexer #(.enable("false")) multiplexer_7 (.in0(jal), .in1(1'b0), .out(multiplexer_7_out), .sel(rst));
  Multiplexer #(.enable("false")) multiplexer_8 (.in0(hault), .in1(1'b0), .out(multiplexer_8_out), .sel(rst));
  Multiplexer #(.enable("false")) multiplexer_9 (.in0(alusrc), .in1(1'b0), .out(multiplexer_9_out), .sel(rst));
  Multiplexer #(.enable("false")) multiplexer_10 (.in0(rw_enable), .in1(1'b0), .out(multiplexer_10_out), .sel(rst));
  Multiplexer #(.width(5), .enable("false")) multiplexer_11 (
    .in0(rW), .in1({5{1'b0}}), .out(multiplexer_11_out), .sel(rst));
  Multiplexer #(.width(4), .enable("false")) multiplexer_12 (
    .in0(aluop), .in1(4'b0000), .out(multiplexer_12_out), .sel(rst));
  Register_part #(.width(1)) register_7 (.D(multiplexer_7_out), .en(enable), .Q(jal_2), .clk(clk));  // open: clr
  Register_part #(.width(1)) register_8 (.D(multiplexer_8_out), .en(enable), .Q(hault_2), .clk(clk));  // open: clr
  Register_part #(.width(1)) register_9 (.D(multiplexer_9_out), .en(enable), .Q(alusrc_2), .clk(clk));  // open: clr
  Register_part #(.width(1)) register_10 (
    .D(multiplexer_10_out), .en(enable), .Q(rw_enable_2), .clk(clk));  // open: clr
  Register_part #(.width(5)) register_11 (.D(multiplexer_11_out), .en(enable), .Q(rW_out), .clk(clk));  // open: clr
  Register_part #(.width(4)) register_12 (.D(multiplexer_12_out), .en(enable), .Q(aluop_out), .clk(clk));  // open: clr
  Multiplexer #(.enable("false")) multiplexer_13 (.in0(jump), .in1(1'b0), .out(multiplexer_13_out), .sel(rst));
  Multiplexer #(.enable("false")) multiplexer_14 (.in0(beq), .in1(1'b0), .out(multiplexer_14_out), .sel(rst));
  Multiplexer #(.enable("false")) multiplexer_15 (.in0(bne), .in1(1'b0), .out(multiplexer_15_out), .sel(rst));
  Multiplexer #(.enable("false")) multiplexer_16 (.in0(memw), .in1(1'b0), .out(multiplexer_16_out), .sel(rst));
  Multiplexer #(.enable("false")) multiplexer_17 (.in0(jr), .in1(1'b0), .out(multiplexer_17_out), .sel(rst));
  Multiplexer #(.enable("false")) multiplexer_18 (.in0(bltz), .in1(1'b0), .out(multiplexer_18_out), .sel(rst));
  Multiplexer #(.enable("false")) multiplexer_19 (.in0(lh), .in1(1'b0), .out(multiplexer_19_out), .sel(rst));
  Multiplexer #(.enable("false")) multiplexer_20 (.in0(memread), .in1(1'b0), .out(multiplexer_20_out), .sel(rst));
  Register_part #(.width(1)) register_13 (.D(multiplexer_13_out), .en(enable), .Q(jump_out), .clk(clk));  // open: clr
  Register_part #(.width(1)) register_14 (.D(multiplexer_14_out), .en(enable), .Q(beq_out), .clk(clk));  // open: clr
  Register_part #(.width(1)) register_15 (.D(multiplexer_15_out), .en(enable), .Q(bne_out), .clk(clk));  // open: clr
  Register_part #(.width(1)) register_16 (.D(multiplexer_16_out), .en(enable), .Q(memw_out), .clk(clk));  // open: clr
  Register_part #(.width(1)) register_17 (.D(multiplexer_17_out), .en(enable), .Q(jr_out), .clk(clk));  // open: clr
  Register_part #(.width(1)) register_18 (.D(multiplexer_18_out), .en(enable), .Q(bltz_2), .clk(clk));  // open: clr
  Register_part #(.width(1)) register_19 (.D(multiplexer_19_out), .en(enable), .Q(lh_out), .clk(clk));  // open: clr
  Register_part #(.width(1)) register_20 (
    .D(multiplexer_20_out), .en(enable), .Q(mem_read_out), .clk(clk));  // open: clr
endmodule

module ALU (
  input  [31:0] X,
  input  [31:0] Y,
  input  [3:0] ALUOP,
  output [31:0] Result,
  output equal
);

  ALU_part alu_1 (
    .AluOP(ALUOP), .X(X), .Equal(equal), .Result(Result), .Y(Y));  // open: Signed_Overflow, Result_2, UnSigned_Overflow
endmodule

module syscall (
  input  [31:0] RB,
  input  [31:0] RA,
  input  syscall,
  input  clk,
  input  rst,
  output [31:0] syscall_out,
  output hault
);

  wire and_1_out, comparator_1_eq;

  Comparator #(.width(32), .mode("unsigned")) comparator_1 (.a(RA), .b(32'ha), .eq(comparator_1_eq));  // open: gt, lt
  Register_part #(.width(32)) register_1 (.D(RB), .en(and_1_out), .Q(syscall_out), .clk(clk), .clr(rst));
  and and_1 (and_1_out, ~comparator_1_eq, syscall);  // AND_Gate
  and and_2 (hault, comparator_1_eq, syscall);
endmodule

module EX_MEM (
  input  [31:0] RB,
  input  hault,
  input  rw_enable,
  input  [31:0] NPC_in,
  input  memwrite,
  input  lh,
  input  [31:0] IR_in,
  input  memread,
  input  [31:0] result,
  input  [4:0] rW,
  input  clk,
  input  rst,
  output [31:0] RB_out,
  output hault_2,
  output rw_enable_2,
  output [31:0] NPC_out,
  output memwrite_out,
  output lh_out,
  output [31:0] IR_out,
  output memread_out,
  output [31:0] result_out,
  output [4:0] rW_out
);

  Register_part #(.width(32)) register_1 (.D(RB), .Q(RB_out), .clk(clk), .clr(rst));  // open: en
  Register_part #(.width(32)) register_2 (.D(NPC_in), .Q(NPC_out), .clk(clk), .clr(rst));  // open: en
  Register_part #(.width(32)) register_3 (.D(IR_in), .Q(IR_out), .clk(clk), .clr(rst));  // open: en
  Register_part #(.width(32)) register_4 (.D(result), .Q(result_out), .clk(clk), .clr(rst));  // open: en
  Register_part #(.width(1)) register_5 (.D(hault), .Q(hault_2), .clk(clk), .clr(rst));  // open: en
  Register_part #(.width(1)) register_6 (.D(rw_enable), .Q(rw_enable_2), .clk(clk), .clr(rst));  // open: en
  Register_part #(.width(1)) register_7 (.D(memwrite), .Q(memwrite_out), .clk(clk), .clr(rst));  // open: en
  Register_part #(.width(1)) register_8 (.D(lh), .Q(lh_out), .clk(clk), .clr(rst));  // open: en
  Register_part #(.width(1)) register_9 (.D(memread), .Q(memread_out), .clk(clk), .clr(rst));  // open: en
  Register_part #(.width(5)) register_10 (.D(rW), .Q(rW_out), .clk(clk), .clr(rst));  // open: en
endmodule

module MEM_WB (
  input  hault,
  input  rw_select,
  input  rw_enable,
  input  [4:0] rW,
  input  [31:0] alu_result,
  input  [31:0] mem_value,
  input  clk,
  input  rst,
  output hault_2,
  output rw_select_2,
  output rw_enable_2,
  output [4:0] rW_out,
  output [31:0] alu_result_2,
  output [31:0] mem_value_2
);

  Register_part #(.width(1)) register_1 (.D(hault), .Q(hault_2), .clk(clk), .clr(rst));  // open: en
  Register_part #(.width(1)) register_2 (.D(rw_select), .Q(rw_select_2), .clk(clk), .clr(rst));  // open: en
  Register_part #(.width(1)) register_3 (.D(rw_enable), .Q(rw_enable_2), .clk(clk), .clr(rst));  // open: en
  Register_part #(.width(5)) register_4 (.D(rW), .Q(rW_out), .clk(clk), .clr(rst));  // open: en
  Register_part #(.width(32)) register_5 (.D(alu_result), .Q(alu_result_2), .clk(clk), .clr(rst));  // open: en
  Register_part #(.width(32)) register_6 (.D(mem_value), .Q(mem_value_2), .clk(clk), .clr(rst));  // open: en
endmodule

module PredictPC (
  input  JMP,
  input  bSucces,
  input  [31:0] pc,
  input  [31:0] next_pc,
  output [31:0] pc_out
);

  wire or_1_out;
  wire [31:0] adder_1_out;

  Adder #(.width(32)) adder_1 (.a(pc), .b(32'h4), .out(adder_1_out));  // open: cin, cout
  or or_1 (or_1_out, JMP, bSucces);
  Multiplexer #(.width(32), .enable("false")) multiplexer_1 (
    .in0(adder_1_out), .in1(next_pc), .out(pc_out), .sel(or_1_out));
endmodule

module Bubble (
  input  rBvalid,
  input  [4:0] rWEX,
  input  rweEX,
  input  [4:0] rA,
  input  [4:0] rB,
  input  [4:0] rWMEM,
  input  rweMEM,
  input  JMP,
  output stall,
  output BubId,
  output BubIf
);

  wire and_1_out, and_2_out, and_3_out, and_4_out, comparator_1_eq, comparator_2_eq, comparator_3_eq,
       comparator_4_eq, comparator_5_eq, comparator_6_eq, not_1_out, not_2_out;

  Comparator #(.width(5), .mode("unsigned")) comparator_1 (
    .a(rWEX), .b({5{1'b0}}), .eq(comparator_1_eq));  // open: gt, lt
  Comparator #(.width(5), .mode("unsigned")) comparator_2 (.a(rWEX), .b(rA), .eq(comparator_2_eq));  // open: gt, lt
  Comparator #(.width(5), .mode("unsigned")) comparator_3 (.a(rWEX), .b(rB), .eq(comparator_3_eq));  // open: gt, lt
  Comparator #(.width(5), .mode("unsigned")) comparator_4 (
    .a(rWMEM), .b({5{1'b0}}), .eq(comparator_4_eq));  // open: gt, lt
  Comparator #(.width(5), .mode("unsigned")) comparator_5 (.a(rWMEM), .b(rA), .eq(comparator_5_eq));  // open: gt, lt
  Comparator #(.width(5), .mode("unsigned")) comparator_6 (.a(rWMEM), .b(rB), .eq(comparator_6_eq));  // open: gt, lt
  not not_1 (not_1_out, comparator_1_eq);
  not not_2 (not_2_out, comparator_4_eq);
  and and_1 (and_1_out, not_1_out, rweEX, comparator_2_eq);
  and and_2 (and_2_out, not_1_out, rweEX, comparator_3_eq, rBvalid);
  and and_3 (and_3_out, not_2_out, rweMEM, comparator_5_eq);
  and and_4 (and_4_out, not_2_out, rweMEM, comparator_6_eq, rBvalid);
  or or_1 (stall, and_1_out, and_2_out, and_3_out, and_4_out);
  or or_2 (BubId, stall, JMP);

  assign BubIf = JMP;
endmodule
