// Logisim project 简单流水线.circ as structural Verilog: 12 circuits, main circuit cpu
module cpu (
);

  wire alu_1_equal, and_1_out, and_2_out, and_3_out, and_4_out, and_5_out, and_6_out, beq, bgez, bne, clk,
       cmp, conti, control_1_alusrc, control_1_beq, control_1_bltz, control_1_bne, control_1_jal,
       control_1_jr, control_1_jump, control_1_memread, control_1_memwrite, control_1_regdst,
       control_1_regwrite, control_1_shift, control_1_syscall, control_1_zero_extend, counter_4_q, equal,
       ex_mem_1_hault_2, ex_mem_1_memread_out, ex_mem_1_memwrite_out, ex_mem_1_rw_enable_2, hault,
       id_ex_1_alusrc_2, id_ex_1_beq_out, id_ex_1_bltz_2, id_ex_1_bne_out, id_ex_1_hault_2, id_ex_1_jr_out,
       id_ex_1_jump_out, id_ex_1_mem_read_out, id_ex_1_memw_out, id_ex_1_rw_enable_2, Jal, Jr, Jump,
       mem_wb_1_rw_select_2, not_1_out, not_2_out, or_1_out, or_2_out, or_3_out, or_4_out, pcEnable, RST,
       rw_enable, syscall_1_hault;
  wire [3:0] control_1_aluop, control_1_lh, ex_mem_1_lh_out, id_ex_1_aluop_out, id_ex_1_lh_out;
  wire [4:0] decoder_1_ra, decoder_1_rb, decoder_1_rw, ex_mem_1_rw_out, id_ex_1_rw_out, rW;
  wire [5:0] decoder_1_funct, decoder_1_opcode;
  wire [15:0] \总周期数 , \无条件分支指令数 , \有条件分支成功跳转 , \有条件分支指令数 ;
  wire [19:0] ex_mem_1_result_out_2;
  wire [31:0] adder_1_out, alu_1_result, decoder_1_extend, decoder_1_pcjump, ex_mem_1_rb_out,
       ex_mem_1_result_out, id_ex_1_imm_out, id_ex_1_ir_out, id_ex_1_npc_out, id_ex_1_pcjump_out,
       id_ex_1_ra_out, id_ex_1_rb_out, if_id_1_ir_out, if_id_1_npc_out, mem_wb_1_alu_result_2,
       mem_wb_1_mem_value_2, mips_ram_1_p8, multiplexer_1_out, multiplexer_2_out, multiplexer_3_out, pc_q,
       register_1_ra_2, register_1_rb_2, rom_1_data, syso;

  Button \u_总复位  (.out(RST));
  Hex_Digit_Display hex_digit_display_1 (.value(syso[31:28]));  // open: dp
  Hex_Digit_Display hex_digit_display_2 (.value(syso[27:24]));  // open: dp
  Register_part #(.width(32)) pc (.D(adder_1_out), .en(not_1_out), .Q(pc_q), .clk(clk), .clr(RST));
  not not_1 (not_1_out, hault);
  Hex_Digit_Display hex_digit_display_3 (.value(syso[23:20]));  // open: dp
  Hex_Digit_Display hex_digit_display_4 (.value(syso[19:16]));  // open: dp
  Adder #(.width(32)) adder_1 (.a(32'h4), .b(pc_q), .out(adder_1_out));  // open: cin, cout
  Hex_Digit_Display hex_digit_display_5 (.value(syso[11:8]));  // open: dp
  Hex_Digit_Display hex_digit_display_6 (.value(syso[15:12]));  // open: dp
  Multiplexer #(.width(32), .enable("false")) multiplexer_1 (
    .in1(adder_1_out), .out(multiplexer_1_out));  // open: in0, sel
  ROM #(.addrWidth(10), .dataWidth(32)) rom_1 (.addr(pc_q[11:2]), .data(rom_1_data));  // open: sel
  Hex_Digit_Display hex_digit_display_7 (.value(syso[7:4]));  // open: dp
  Hex_Digit_Display hex_digit_display_8 (.value(syso[3:0]));  // open: dp
  Clock clock_1 (.out(clk));
  Button Continue (.out(conti));
  IF_ID if_id_1 (
    .NPC_in(multiplexer_1_out), .IR_in(rom_1_data), .NPC_out(if_id_1_npc_out), .IR_out(if_id_1_ir_out),
    .clk(clk), .rst(RST));
  Decoder decoder_1 (
    .CODE(if_id_1_ir_out), .PCjump(decoder_1_pcjump), .OPCODE(decoder_1_opcode), .FUNCT(decoder_1_funct),
    .RA(decoder_1_ra), .RB(decoder_1_rb), .shift(control_1_shift), .syscall(control_1_syscall),
    .Zero_extend(control_1_zero_extend), .extend(decoder_1_extend), .rW(decoder_1_rw),
    .RegDst(control_1_regdst), .Jal(control_1_jal));
  Register register_1 (
    .w(multiplexer_3_out), .clk(not_2_out), .we(rw_enable), .rw(rW), .ra(decoder_1_ra), .rb(decoder_1_rb),
    .RA_2(register_1_ra_2), .RB_2(register_1_rb_2));
  not not_2 (not_2_out, clk);
  // Probe on \总周期数 
  Control control_1 (
    .ALUOP(control_1_aluop), .shift(control_1_shift), .Zero_extend(control_1_zero_extend),
    .ALUSrc(control_1_alusrc), .RegDst(control_1_regdst), .RegWrite(control_1_regwrite),
    .Jump(control_1_jump), .beq(control_1_beq), .bne(control_1_bne), .MemWrite(control_1_memwrite),
    .Jal(control_1_jal), .jr(control_1_jr), .syscall(control_1_syscall), .bltz(control_1_bltz),
    .OPCODE(decoder_1_opcode), .FUNCT(decoder_1_funct), .lh(control_1_lh), .memread(control_1_memread));
  syscall syscall_1 (
    .RA(register_1_ra_2), .syscall(control_1_syscall), .syscall_out(syso), .hault(syscall_1_hault),
    .RB(register_1_rb_2), .clk(clk), .rst(RST), .\continue (conti));
  or or_1 (or_1_out, Jal, Jump, Jr);
  or or_2 (or_2_out, bne, beq, bgez);
  and and_1 (and_1_out, bne, ~equal);  // AND_Gate
  and and_2 (and_2_out, equal, beq);
  or or_3 (or_3_out, and_1_out, and_2_out, and_3_out);
  and and_3 (and_3_out, bgez, cmp);
  ID_EX id_ex_1 (
    .jump(control_1_jump), .beq(control_1_beq), .bne(control_1_bne), .memw(control_1_memwrite),
    .NPC_in(if_id_1_npc_out), .aluop(control_1_aluop), .jr(control_1_jr), .alusrc(control_1_alusrc),
    .bltz(control_1_bltz), .IR_in(if_id_1_ir_out), .rw_enable(control_1_regwrite), .lh(control_1_lh),
    .jump_out(id_ex_1_jump_out), .beq_out(id_ex_1_beq_out), .bne_out(id_ex_1_bne_out),
    .memw_out(id_ex_1_memw_out), .NPC_out(id_ex_1_npc_out), .aluop_out(id_ex_1_aluop_out),
    .jr_out(id_ex_1_jr_out), .alusrc_2(id_ex_1_alusrc_2), .bltz_2(id_ex_1_bltz_2), .IR_out(id_ex_1_ir_out),
    .rw_enable_2(id_ex_1_rw_enable_2), .lh_out(id_ex_1_lh_out), .clk(clk), .rst(RST), .imm(decoder_1_extend),
    .imm_out(id_ex_1_imm_out), .pcjump(decoder_1_pcjump), .pcjump_out(id_ex_1_pcjump_out),
    .RA(register_1_ra_2), .RA_out(id_ex_1_ra_out), .RB(register_1_rb_2), .RB_out(id_ex_1_rb_out),
    .memread(control_1_memread), .mem_read_out(id_ex_1_mem_read_out), .rW(decoder_1_rw),
    .rW_out(id_ex_1_rw_out), .hault(syscall_1_hault), .hault_2(id_ex_1_hault_2));
  Counter #(.width(16), .max('hffff)) counter_1 (
    .count(and_4_out), .Q(\无条件分支指令数 ), .clk(clk), .clr(RST));  // open: load, D, carry
  and and_4 (and_4_out, or_1_out, pcEnable);
  Counter #(.width(16), .max('hffff)) counter_2 (
    .count(and_5_out), .Q(\有条件分支指令数 ), .clk(clk), .clr(RST));  // open: load, D, carry
  and and_5 (and_5_out, or_2_out, pcEnable);
  Counter #(.width(16), .max('hffff)) counter_3 (
    .count(and_6_out), .Q(\有条件分支成功跳转 ), .clk(clk), .clr(RST));  // open: load, D, carry
  and and_6 (and_6_out, pcEnable, or_3_out);
  Npc npc_1 (
    .PCjmp(id_ex_1_pcjump_out), .jump(id_ex_1_jump_out), .extendIMM(id_ex_1_imm_out), .bne(id_ex_1_bne_out),
    .beq(id_ex_1_beq_out), .PC_4(id_ex_1_npc_out), .jr(id_ex_1_jr_out), .dA(id_ex_1_ra_out),
    .equal(alu_1_equal), .bltz(id_ex_1_bltz_2));  // open: NextPc
  ALU alu_1 (
    .X(id_ex_1_ra_out), .Y(multiplexer_2_out), .Result(alu_1_result), .ALUOP(id_ex_1_aluop_out),
    .equal(alu_1_equal));
  Multiplexer #(.width(32), .enable("false")) multiplexer_2 (
    .in0(id_ex_1_rb_out), .in1(id_ex_1_imm_out), .out(multiplexer_2_out), .sel(id_ex_1_alusrc_2));
  EX_MEM ex_mem_1 (
    .result(alu_1_result),
    .result_out({ex_mem_1_result_out[31:22], ex_mem_1_result_out_2, ex_mem_1_result_out[1:0]}), .clk(clk),
    .rst(RST), .NPC_in(id_ex_1_npc_out), .IR_in(id_ex_1_ir_out), .memread(id_ex_1_mem_read_out),
    .memread_out(ex_mem_1_memread_out), .rW(id_ex_1_rw_out), .rW_out(ex_mem_1_rw_out),
    .memwrite(id_ex_1_memw_out), .memwrite_out(ex_mem_1_memwrite_out), .lh(id_ex_1_lh_out),
    .lh_out(ex_mem_1_lh_out), .rw_enable(id_ex_1_rw_enable_2), .rw_enable_2(ex_mem_1_rw_enable_2),
    .RB(id_ex_1_rb_out), .RB_out(ex_mem_1_rb_out), .hault(id_ex_1_hault_2), .hault_2(ex_mem_1_hault_2));  // open: NPC_out, IR_out
  // MIPS_RAM mips_ram_1: pin names not known; wires that end beside it: {ex_mem_1_result_out[31:22], ex_mem_1_result_out_2, ex_mem_1_result_out[1:0]}, ex_mem_1_result_out_2, ex_mem_1_rb_out, ex_mem_1_memwrite_out, ex_mem_1_lh_out, clk, RST, mips_ram_1_p8
  Counter #(.width(1), .max('h1)) counter_4 (
    .count(hault), .Q(counter_4_q), .clk(clk), .clr(or_4_out));  // open: load, D, carry
  or or_4 (or_4_out, conti, RST);
  MEM_WB mem_wb_1 (
    .alu_result({ex_mem_1_result_out[31:22], ex_mem_1_result_out_2, ex_mem_1_result_out[1:0]}),
    .alu_result_2(mem_wb_1_alu_result_2), .mem_value(mips_ram_1_p8), .mem_value_2(mem_wb_1_mem_value_2),
    .clk(clk), .rst(RST), .rW(ex_mem_1_rw_out), .rW_out(rW), .rw_enable(ex_mem_1_rw_enable_2),
    .rw_enable_2(rw_enable), .rw_select(ex_mem_1_memread_out), .rw_select_2(mem_wb_1_rw_select_2),
    .hault(ex_mem_1_hault_2), .hault_2(hault));
  Counter #(.width(16), .max('hffff)) counter_5 (
    .count(pcEnable), .Q(\总周期数 ), .clk(clk), .clr(RST));  // open: load, D, carry
  not not_3 (pcEnable, counter_4_q);
  Multiplexer #(.width(32), .enable("false")) multiplexer_3 (
    .in0(mem_wb_1_alu_result_2), .in1(mem_wb_1_mem_value_2), .out(multiplexer_3_out),
    .sel(mem_wb_1_rw_select_2));

  // Notes on the sheet:
  //   数码管输出应该用寄存器锁存，否则显示数据只能一闪而过
  //   可以通过项目增加Logisim库的方式将前几次实验完成的电路作为子电路引入到本电路中使用
  //   指令存储器
  //   contents of rom_1 (hex, n*v repeats v):
  //   20100000 20110000 20120000 20130000 36100000 36310001 36520002 36730003 ae100000 ae110004 ae120008
  //   ae13000c 2002000a 20110000 20120000 20130000 c
  //   数码管输出
  //   总复位信号应将除ROM以外所有存储组件全部清零
endmodule

module Control (
  input  [5:0] OPCODE,
  input  [5:0] FUNCT,
  output [3:0] ALUOP,
  output shift,
  output ALUSrc,
  output Zero_extend,
  output RegDst,
  output Jump,
  output RegWrite,
  output beq,
  output bne,
  output MemWrite,
  output Jal,
  output jr,
  output syscall,
  output bltz,
  output memread,
  output [3:0] lh
);

  wire add, addi, addiu, addu, \and , andi, comparator_1_eq, comparator_16_eq, comparator_17_eq,
       comparator_18_eq, comparator_19_eq, comparator_20_eq, comparator_21_eq, comparator_22_eq,
       comparator_23_eq, comparator_24_eq, comparator_25_eq, comparator_26_eq, comparator_27_eq,
       comparator_28_eq, comparator_29_eq, j, lh_t, lw, \nor , \or , or_1_out, or_2_out, or_3_out, or_4_out,
       or_9_out, ori, sll, slt, slti, sltu, sra, srl, sub, subu, xori;

  Comparator #(.width(6)) comparator_1 (.a(OPCODE), .b({6{1'b0}}), .eq(comparator_1_eq));  // open: gt, lt
  Comparator #(.width(6)) comparator_2 (.a(OPCODE), .b(6'b001000), .eq(addi));  // open: gt, lt
  Comparator #(.width(6)) comparator_3 (.a(OPCODE), .b(6'b001001), .eq(addiu));  // open: gt, lt
  Comparator #(.width(6)) comparator_4 (.a(OPCODE), .b(6'b001100), .eq(andi));  // open: gt, lt
  Comparator #(.width(6)) comparator_5 (.a(OPCODE), .b(6'b001101), .eq(ori));  // open: gt, lt
  Comparator #(.width(6)) comparator_6 (.a(OPCODE), .b(6'b100011), .eq(lw));  // open: gt, lt
  Comparator #(.width(6)) comparator_7 (.a(OPCODE), .b(6'b101011), .eq(MemWrite));  // open: gt, lt
  Comparator #(.width(6)) comparator_8 (.a(OPCODE), .b(6'b000100), .eq(beq));  // open: gt, lt
  Comparator #(.width(6)) comparator_9 (.a(OPCODE), .b(6'b000101), .eq(bne));  // open: gt, lt
  Comparator #(.width(6)) comparator_10 (.a(OPCODE), .b(6'b001010), .eq(slti));  // open: gt, lt
  Comparator #(.width(6)) comparator_11 (.a(OPCODE), .b(6'b000010), .eq(j));  // open: gt, lt
  Comparator #(.width(6)) comparator_12 (.a(OPCODE), .b(6'b000011), .eq(Jal));  // open: gt, lt
  Comparator #(.width(6)) comparator_13 (.a(OPCODE), .b(6'b001110), .eq(xori));  // open: gt, lt
  Comparator #(.width(6)) comparator_14 (.a(OPCODE), .b(6'b100001), .eq(lh_t));  // open: gt, lt
  Comparator #(.width(6)) comparator_15 (.a(OPCODE), .b(6'b000001), .eq(bltz));  // open: gt, lt
  Comparator #(.width(6)) comparator_16 (.a(FUNCT), .b(6'b100000), .eq(comparator_16_eq));  // open: gt, lt
  Comparator #(.width(6)) comparator_17 (.a(FUNCT), .b(6'b100001), .eq(comparator_17_eq));  // open: gt, lt
  Comparator #(.width(6)) comparator_18 (.a(FUNCT), .b(6'b100100), .eq(comparator_18_eq));  // open: gt, lt
  Comparator #(.width(6)) comparator_19 (.a(FUNCT), .b({6{1'b0}}), .eq(comparator_19_eq));  // open: gt, lt
  Comparator #(.width(6)) comparator_20 (.a(FUNCT), .b(6'b000011), .eq(comparator_20_eq));  // open: gt, lt
  Comparator #(.width(6)) comparator_21 (.a(FUNCT), .b(6'b000010), .eq(comparator_21_eq));  // open: gt, lt
  Comparator #(.width(6)) comparator_22 (.a(FUNCT), .b(6'b100010), .eq(comparator_22_eq));  // open: gt, lt
  Comparator #(.width(6)) comparator_23 (.a(FUNCT), .b(6'b100101), .eq(comparator_23_eq));  // open: gt, lt
  Comparator #(.width(6)) comparator_24 (.a(FUNCT), .b(6'b100111), .eq(comparator_24_eq));  // open: gt, lt
  Comparator #(.width(6)) comparator_25 (.a(FUNCT), .b(6'b101010), .eq(comparator_25_eq));  // open: gt, lt
  Comparator #(.width(6)) comparator_26 (.a(FUNCT), .b(6'b101011), .eq(comparator_26_eq));  // open: gt, lt
  Comparator #(.width(6)) comparator_27 (.a(FUNCT), .b(6'b001000), .eq(comparator_27_eq));  // open: gt, lt
  Comparator #(.width(6)) comparator_28 (.a(FUNCT), .b(6'b001100), .eq(comparator_28_eq));  // open: gt, lt
  Comparator #(.width(6)) comparator_29 (.a(FUNCT), .b(6'b100011), .eq(comparator_29_eq));  // open: gt, lt
  and and_1 (add, comparator_1_eq, comparator_16_eq);
  and and_2 (addu, comparator_1_eq, comparator_17_eq);
  and and_3 (\and , comparator_1_eq, comparator_18_eq);
  and and_4 (sll, comparator_1_eq, comparator_19_eq);
  and and_5 (sra, comparator_1_eq, comparator_20_eq);
  and and_6 (srl, comparator_1_eq, comparator_21_eq);
  and and_7 (sub, comparator_1_eq, comparator_22_eq);
  and and_8 (\or , comparator_1_eq, comparator_23_eq);
  and and_9 (\nor , comparator_1_eq, comparator_24_eq);
  and and_10 (slt, comparator_1_eq, comparator_25_eq);
  and and_11 (sltu, comparator_1_eq, comparator_26_eq);
  and and_12 (jr, comparator_1_eq, comparator_27_eq);
  and and_13 (syscall, comparator_1_eq, comparator_28_eq);
  and and_14 (subu, comparator_1_eq, comparator_29_eq);
  or or_1 (or_1_out, sub, subu);
  or or_2 (or_2_out, \and , andi);
  or or_3 (or_3_out, \or , ori);
  or or_4 (or_4_out, slt, slti);
  or or_5 (shift, sll, sra, srl);
  or or_6 (Zero_extend, xori, andi, ori);
  or or_7 (RegDst, add, \nor , addu, \and , sll, sra, srl, \or , slt, sltu, subu, sub);
  or or_8 (Jump, j, Jal);
  Multiplexer #(.width(4), .enable("false")) multiplexer_1 (.in0(4'b1111), .in1(4'b0011), .out(lh), .sel(lh_t));
  or or_9 (or_9_out, add, addi, addiu, addu, lw, MemWrite, beq, bne, bltz, lh_t);
  Priority_Encoder #(.select(4)) priority_encoder_1 (
    .in0(sll), .in1(sra), .in2(srl), .in3(1'b0), .in4(1'b0), .in5(or_9_out), .in6(or_1_out), .in7(or_2_out),
    .in8(or_3_out), .in9(xori), .in10(\nor ), .in11(or_4_out), .in12(sltu), .in13(1'b0), .in14(1'b0),
    .in15(1'b0), .out(ALUOP));  // open: gs, en_out, en_in
  or or_10 (ALUSrc, addi, addiu, andi, sll, sra, srl, ori, lw, MemWrite, slti, xori, lh_t);
  or or_11 (RegWrite, slt, add, addiu, addu, \and , sll, sra, \nor , srl, \or , lh_t, sltu, subu, sub, addi, andi, ori, lw, slti, xori, Jal);
  or or_12 (memread, lw, lh_t);

  // Other names for the same wires on the sheet: sw = MemWrite
endmodule

module Decoder (
  input  [31:0] CODE,
  input  shift,
  input  syscall,
  input  RegDst,
  input  Jal,
  input  Zero_extend,
  output [31:0] PCjump,
  output [5:0] OPCODE,
  output [5:0] FUNCT,
  output [4:0] RA,
  output [4:0] RB,
  output [4:0] rW,
  output [31:0] extend
);

  wire [4:0] multiplexer_1_out, multiplexer_2_out;
  wire [31:0] bit_extender_1_out, bit_extender_2_out, bit_extender_3_out, multiplexer_6_out;

  Shifter #(.width(28)) shifter_1 (.in(CODE[27:0]), .\dist (5'b00010), .out(PCjump[27:0]));
  Multiplexer #(.width(5), .enable("false")) multiplexer_1 (
    .in0(CODE[25:21]), .in1(CODE[20:16]), .out(multiplexer_1_out), .sel(shift));
  Multiplexer #(.width(5), .enable("false")) multiplexer_2 (
    .in0(CODE[20:16]), .in1(CODE[15:11]), .out(multiplexer_2_out), .sel(RegDst));
  Multiplexer #(.width(5), .enable("false")) multiplexer_3 (
    .in0(multiplexer_1_out), .in1(5'b00010), .out(RA), .sel(syscall));
  Multiplexer #(.width(5), .enable("false")) multiplexer_4 (
    .in0(multiplexer_2_out), .in1({5{1'b1}}), .out(rW), .sel(Jal));
  assign bit_extender_1_out = {{16{CODE[15]}}, CODE[15:0]};  // Bit_Extender bit_extender_1
  assign bit_extender_2_out = {{16{1'b0}}, CODE[15:0]};  // Bit_Extender bit_extender_2
  assign bit_extender_3_out = {{27{1'b0}}, CODE[10:6]};  // Bit_Extender bit_extender_3
  Multiplexer #(.width(5), .enable("false")) multiplexer_5 (.in0(CODE[20:16]), .in1(5'b00100), .out(RB), .sel(syscall));
  Multiplexer #(.width(32), .enable("false")) multiplexer_6 (
    .in0(bit_extender_1_out), .in1(bit_extender_2_out), .out(multiplexer_6_out), .sel(Zero_extend));
  Multiplexer #(.width(32), .enable("false")) multiplexer_7 (
    .in0(multiplexer_6_out), .in1(bit_extender_3_out), .out(extend), .sel(shift));

  assign FUNCT = CODE[5:0];
  assign OPCODE = CODE[31:26];
  assign PCjump[31:28] = 4'b0000;
endmodule

// NPC
module Npc (
  input  jr,
  input  [31:0] dA,
  input  [31:0] PCjmp,
  input  jump,
  input  bltz,
  input  bne,
  input  equal,
  input  beq,
  input  [31:0] PC_4,
  input  [31:0] extendIMM,
  output [31:0] NextPc
);

  wire and_1_out, and_2_out, and_3_out, cmp, comparator_1_gt, or_1_out;
  wire [31:0] adder_1_out, multiplexer_2_out, multiplexer_3_out, shifter_1_out;

  Multiplexer #(.width(32), .enable("false")) multiplexer_1 (.in0(multiplexer_2_out), .in1(dA), .out(NextPc), .sel(jr));
  Shifter #(.width(32)) shifter_1 (.in(extendIMM), .\dist (5'b00010), .out(shifter_1_out));
  not not_1 (cmp, comparator_1_gt);
  Comparator #(.width(32)) comparator_1 (.a({32{1'b0}}), .b(dA), .gt(comparator_1_gt));  // open: eq, lt
  Adder #(.width(32)) adder_1 (.a(PC_4), .b(shifter_1_out), .out(adder_1_out));  // open: cin, cout
  Multiplexer #(.width(32), .enable("false")) multiplexer_2 (
    .in0(multiplexer_3_out), .in1({PC_4[31:28], PCjmp[27:0]}), .out(multiplexer_2_out), .sel(jump));
  and and_1 (and_1_out, bltz, cmp);
  Multiplexer #(.width(32), .enable("false")) multiplexer_3 (
    .in0(PC_4), .in1(adder_1_out), .out(multiplexer_3_out), .sel(or_1_out));
  or or_1 (or_1_out, and_1_out, and_2_out, and_3_out);
  and and_2 (and_2_out, bne, ~equal);  // AND_Gate
  and and_3 (and_3_out, equal, beq);
endmodule

module IF_ID (
  input  [31:0] NPC_in,
  input  [31:0] IR_in,
  input  clk,
  input  rst,
  output [31:0] NPC_out,
  output [31:0] IR_out
);

  Register_part #(.width(32)) register_1 (.D(NPC_in), .Q(NPC_out), .clk(clk), .clr(rst));  // open: en
  Register_part #(.width(32)) register_2 (.D(IR_in), .Q(IR_out), .clk(clk), .clr(rst));  // open: en
endmodule

// Reg
module Register (
  input  [31:0] w,
  input  clk,
  input  we,
  input  [4:0] rw,
  input  [4:0] ra,
  input  [4:0] rb,
  output [31:0] RA_2,
  output [31:0] RB_2
);

  // RegisterFile registerfile_1: pin names not known; wires that end beside it: w, clk, we, rw, ra, rb, RA_2, RB_2
endmodule

module test (
  input  [31:0] CODE,
  input  RegDst,
  input  Jal,
  output [4:0] RW
);

  wire [4:0] multiplexer_1_out, undriven;

  Multiplexer #(.width(5), .enable("false")) multiplexer_1 (
    .in0(undriven), .in1(CODE[15:11]), .out(multiplexer_1_out), .sel(RegDst));
  Multiplexer #(.width(5), .enable("false")) multiplexer_2 (
    .in0(multiplexer_1_out), .in1({5{1'b1}}), .out(RW), .sel(Jal));
endmodule

module ID_EX (
  input  [31:0] imm,
  input  jump,
  input  [31:0] pcjump,
  input  beq,
  input  [31:0] NPC_in,
  input  hault,
  input  bne,
  input  [4:0] rW,
  input  memw,
  input  [31:0] IR_in,
  input  [3:0] aluop,
  input  jr,
  input  alusrc,
  input  bltz,
  input  [31:0] RA,
  input  rw_enable,
  input  [3:0] lh,
  input  [31:0] RB,
  input  memread,
  input  clk,
  input  rst,
  output [31:0] imm_out,
  output jump_out,
  output [31:0] pcjump_out,
  output beq_out,
  output [31:0] NPC_out,
  output hault_2,
  output bne_out,
  output [4:0] rW_out,
  output memw_out,
  output [31:0] IR_out,
  output [3:0] aluop_out,
  output jr_out,
  output alusrc_2,
  output bltz_2,
  output [31:0] RA_out,
  output rw_enable_2,
  output [3:0] lh_out,
  output [31:0] RB_out,
  output mem_read_out
);

  Register_part #(.width(32)) register_1 (.D(imm), .Q(imm_out), .clk(clk), .clr(rst));  // open: en
  Register_part #(.width(32)) register_2 (.D(pcjump), .Q(pcjump_out), .clk(clk), .clr(rst));  // open: en
  Register_part #(.width(32)) register_3 (.D(NPC_in), .Q(NPC_out), .clk(clk), .clr(rst));  // open: en
  Register_part #(.width(32)) register_4 (.D(IR_in), .Q(IR_out), .clk(clk), .clr(rst));  // open: en
  Register_part #(.width(32)) register_5 (.D(RA), .Q(RA_out), .clk(clk), .clr(rst));  // open: en
  Register_part #(.width(32)) register_6 (.D(RB), .Q(RB_out), .clk(clk), .clr(rst));  // open: en
  Register_part #(.width(1)) register_7 (.D(hault), .Q(hault_2), .clk(clk), .clr(rst));  // open: en
  Register_part #(.width(5)) register_8 (.D(rW), .Q(rW_out), .clk(clk), .clr(rst));  // open: en
  Register_part #(.width(4)) register_9 (.D(aluop), .Q(aluop_out), .clk(clk), .clr(rst));  // open: en
  Register_part #(.width(1)) register_10 (.D(alusrc), .Q(alusrc_2), .clk(clk), .clr(rst));  // open: en
  Register_part #(.width(1)) register_11 (.D(rw_enable), .Q(rw_enable_2), .clk(clk), .clr(rst));  // open: en
  Register_part #(.width(1)) register_12 (.D(jump), .Q(jump_out), .clk(clk), .clr(rst));  // open: en
  Register_part #(.width(1)) register_13 (.D(beq), .Q(beq_out), .clk(clk), .clr(rst));  // open: en
  Register_part #(.width(1)) register_14 (.D(bne), .Q(bne_out), .clk(clk), .clr(rst));  // open: en
  Register_part #(.width(1)) register_15 (.D(memw), .Q(memw_out), .clk(clk), .clr(rst));  // open: en
  Register_part #(.width(1)) register_16 (.D(jr), .Q(jr_out), .clk(clk), .clr(rst));  // open: en
  Register_part #(.width(1)) register_17 (.D(bltz), .Q(bltz_2), .clk(clk), .clr(rst));  // open: en
  Register_part #(.width(4)) register_18 (.D(lh), .Q(lh_out), .clk(clk), .clr(rst));  // open: en
  Register_part #(.width(1)) register_19 (.D(memread), .Q(mem_read_out), .clk(clk), .clr(rst));  // open: en
endmodule

module ALU (
  input  [31:0] X,
  input  [31:0] Y,
  input  [3:0] ALUOP,
  output [31:0] Result,
  output equal
);

  ALU_part alu_1 (
    .AluOP(ALUOP), .X(X), .Equal(equal), .Result(Result), .Y(Y));  // open: Signed_Overflow, Result_2, UnSigned_Overflow
endmodule

module syscall (
  input  [31:0] RB,
  input  [31:0] RA,
  input  syscall,
  input  clk,
  input  rst,
  input  \continue ,
  output [31:0] syscall_out,
  output hault
);

  wire and_1_out, comparator_1_eq, or_1_out;

  Comparator #(.width(32), .mode("unsigned")) comparator_1 (.a(RA), .b(32'ha), .eq(comparator_1_eq));  // open: gt, lt
  Register_part #(.width(32)) register_1 (.D(RB), .en(and_1_out), .Q(syscall_out), .clk(clk), .clr(or_1_out));
  and and_1 (and_1_out, ~comparator_1_eq, syscall);  // AND_Gate
  and and_2 (hault, comparator_1_eq, syscall);
  or or_1 (or_1_out, rst, \continue );
endmodule

module EX_MEM (
  input  [31:0] RB,
  input  hault,
  input  rw_enable,
  input  [31:0] NPC_in,
  input  memwrite,
  input  [3:0] lh,
  input  [31:0] IR_in,
  input  memread,
  input  [31:0] result,
  input  [4:0] rW,
  input  clk,
  input  rst,
  output [31:0] RB_out,
  output hault_2,
  output rw_enable_2,
  output [31:0] NPC_out,
  output memwrite_out,
  output [3:0] lh_out,
  output [31:0] IR_out,
  output memread_out,
  output [31:0] result_out,
  output [4:0] rW_out
);

  Register_part #(.width(32)) register_1 (.D(RB), .Q(RB_out), .clk(clk), .clr(rst));  // open: en
  Register_part #(.width(32)) register_2 (.D(NPC_in), .Q(NPC_out), .clk(clk), .clr(rst));  // open: en
  Register_part #(.width(32)) register_3 (.D(IR_in), .Q(IR_out), .clk(clk), .clr(rst));  // open: en
  Register_part #(.width(32)) register_4 (.D(result), .Q(result_out), .clk(clk), .clr(rst));  // open: en
  Register_part #(.width(1)) register_5 (.D(hault), .Q(hault_2), .clk(clk), .clr(rst));  // open: en
  Register_part #(.width(1)) register_6 (.D(rw_enable), .Q(rw_enable_2), .clk(clk), .clr(rst));  // open: en
  Register_part #(.width(1)) register_7 (.D(memwrite), .Q(memwrite_out), .clk(clk), .clr(rst));  // open: en
  Register_part #(.width(4)) register_8 (.D(lh), .Q(lh_out), .clk(clk), .clr(rst));  // open: en
  Register_part #(.width(1)) register_9 (.D(memread), .Q(memread_out), .clk(clk), .clr(rst));  // open: en
  Register_part #(.width(5)) register_10 (.D(rW), .Q(rW_out), .clk(clk), .clr(rst));  // open: en
endmodule

module MEM_WB (
  input  hault,
  input  rw_select,
  input  rw_enable,
  input  [4:0] rW,
  input  [31:0] alu_result,
  input  [31:0] mem_value,
  input  clk,
  input  rst,
  output hault_2,
  output rw_select_2,
  output rw_enable_2,
  output [4:0] rW_out,
  output [31:0] alu_result_2,
  output [31:0] mem_value_2
);

  Register_part #(.width(1)) register_1 (.D(hault), .Q(hault_2), .clk(clk), .clr(rst));  // open: en
  Register_part #(.width(1)) register_2 (.D(rw_select), .Q(rw_select_2), .clk(clk), .clr(rst));  // open: en
  Register_part #(.width(1)) register_3 (.D(rw_enable), .Q(rw_enable_2), .clk(clk), .clr(rst));  // open: en
  Register_part #(.width(5)) register_4 (.D(rW), .Q(rW_out), .clk(clk), .clr(rst));  // open: en
  Register_part #(.width(32)) register_5 (.D(alu_result), .Q(alu_result_2), .clk(clk), .clr(rst));  // open: en
  Register_part #(.width(32)) register_6 (.D(mem_value), .Q(mem_value_2), .clk(clk), .clr(rst));  // open: en
endmodule
